// Logisim project circ.circ as structural Verilog: 35 circuits, main circuit main
module main (
  output gnd_buzzer1,
  output high_buzzer_1,
  output gnd_buzzer_2,
  output high_buzzer_2,
  output gnd_buzzer_3,
  output high_buzzer_3
);

  wire alarm_clock_interrupter_1_alarm, and_1_out, Button_down_out, Button_up_out, clock24h_display_1_set_on,
       clock_1_out, decoder_1_out0, decoder_1_out1, decoder_1_out2, decoder_1_out3, decoder_1_out4,
       decoder_1_out5, decoder_1_out6, DipSwitch_1_sw1, DipSwitch_1_sw10, or_1_out, state1_timezone_1_set_on,
       state2_alarmclock_1_alarm_on, state5_game_1_led;
  wire [1:0] state1_timezone_1_timezone;
  wire [2:0] main_statemachine_1_state_binary;
  wire [3:0] demultiplexer_1_out0, demultiplexer_1_out1, demultiplexer_1_out2, demultiplexer_1_out3,
       demultiplexer_1_out4, demultiplexer_1_out5, input_ctrl_1_short;
  wire [6:0] clock24h_display_1_x7_2, clock24h_display_1_x7_3, clock24h_display_1_x7_4,
       clock24h_display_1_x7_5, clock24h_display_1_x7_6, clock24h_display_1_x7_7, DipSwitch_1_sw8,
       multiplexer_1_out, multiplexer_2_out, multiplexer_3_out, multiplexer_4_out, multiplexer_5_out,
       multiplexer_6_out, state1_timezone_1_x7_2, state1_timezone_1_x7_3, state1_timezone_1_x7_5,
       state1_timezone_1_x7_6, state1_timezone_1_x7_7, state2_alarmclock_1_x7_6, state2_alarmclock_1_x7_7,
       state2_alarmclock_1_x7_h1, state2_alarmclock_1_x7_h2, state2_alarmclock_1_x7_m1,
       state2_alarmclock_1_x7_m2, state3_stopwatch_1_x7_0, state3_stopwatch_1_x7_1, state3_stopwatch_1_x7_2,
       state3_stopwatch_1_x7_3, state3_stopwatch_1_x7_4, state3_stopwatch_1_x7_5, state4_countdown_1_x7_2,
       state4_countdown_1_x7_3, state4_countdown_1_x7_4, state4_countdown_1_x7_5, state4_countdown_1_x7_6,
       state4_countdown_1_x7_7, state5_game_1_output_bus_1, state5_game_1_output_bus_2,
       state5_game_1_output_bus_3, state5_game_1_output_bus_4, state6_piano_1_x7_0, state6_piano_1_x7_1,
       state6_piano_1_x7_2, state6_piano_1_x7_3, state6_piano_1_x7_4;

  Clock #(.highDuration(640), .lowDuration(640)) clock_1 (.out(clock_1_out));
  Button Button_up (.out(Button_up_out));
  Button Button_down (.out(Button_down_out));
  DipSwitch #(.number(10)) DipSwitch_1 (
    .sw1(DipSwitch_1_sw1), .sw2(DipSwitch_1_sw8[6]), .sw3(DipSwitch_1_sw8[5]), .sw4(DipSwitch_1_sw8[4]),
    .sw5(DipSwitch_1_sw8[3]), .sw6(DipSwitch_1_sw8[2]), .sw7(DipSwitch_1_sw8[1]), .sw8(DipSwitch_1_sw8[0]),
    .sw10(DipSwitch_1_sw10));  // open: sw9
  input_ctrl input_ctrl_1 (
    .button(Button_up_out), .clk(clock_1_out), .short(input_ctrl_1_short[0]), .long(input_ctrl_1_short[1]));
  input_ctrl input_ctrl_2 (
    .button(Button_down_out), .clk(clock_1_out), .short(input_ctrl_1_short[2]), .long(input_ctrl_1_short[3]));
  main_statemachine main_statemachine_1 (
    .reset(DipSwitch_1_sw10), .alarm(alarm_clock_interrupter_1_alarm), .button1_short(input_ctrl_1_short[0]),
    .button2_short(input_ctrl_1_short[2]), .dippswitch1(DipSwitch_1_sw1), .clk(clock_1_out),
    .state_binary(main_statemachine_1_state_binary));
  Demultiplexer #(.select(3), .width(4), .enable("false")) demultiplexer_1 (
    .out0(demultiplexer_1_out0), .out1(demultiplexer_1_out1), .out2(demultiplexer_1_out2),
    .out3(demultiplexer_1_out3), .out4(demultiplexer_1_out4), .out5(demultiplexer_1_out5),
    .in(input_ctrl_1_short), .sel(main_statemachine_1_state_binary));  // open: out6, out7
  clock24h_display clock24h_display_1 (
    .reset(DipSwitch_1_sw10), .b1_long(demultiplexer_1_out0[1]), .dip_switch(DipSwitch_1_sw1),
    .clk_100ths(clock_1_out), .b1_short(demultiplexer_1_out0[0]), .b2_short(demultiplexer_1_out0[2]),
    .timezone(state1_timezone_1_timezone), .pause(1'b0), .countdown(1'b0), .x7_2(clock24h_display_1_x7_2),
    .x7_3(clock24h_display_1_x7_3), .x7_4(clock24h_display_1_x7_4), .x7_5(clock24h_display_1_x7_5),
    .x7_6(clock24h_display_1_x7_6), .x7_7(clock24h_display_1_x7_7), .set_on(clock24h_display_1_set_on));  // open: x7_0, x7_1
  state6_piano state6_piano_1 (
    .ds1(DipSwitch_1_sw1), .current_state(main_statemachine_1_state_binary), .ds2to7(DipSwitch_1_sw8),
    .high1(high_buzzer_2), .high2(high_buzzer_3), .x7_0(state6_piano_1_x7_0), .x7_1(state6_piano_1_x7_1),
    .x7_2(state6_piano_1_x7_2), .x7_3(state6_piano_1_x7_3), .x7_4(state6_piano_1_x7_4));
  state1_timezone state1_timezone_1 (
    .b1_long(demultiplexer_1_out1[1]), .dip_switch(DipSwitch_1_sw1), .b1_short(demultiplexer_1_out1[0]),
    .b2_short(demultiplexer_1_out1[2]), .clk_100th(clock_1_out), .reset(DipSwitch_1_sw10),
    .x7_7(state1_timezone_1_x7_7), .x7_6(state1_timezone_1_x7_6), .x7_5(state1_timezone_1_x7_5),
    .x7_3(state1_timezone_1_x7_3), .x7_2(state1_timezone_1_x7_2), .timezone(state1_timezone_1_timezone),
    .set_on(state1_timezone_1_set_on));
  state4_countdown state4_countdown_1 (
    .b1_long(demultiplexer_1_out4[1]), .dip_switch(DipSwitch_1_sw1), .b1_short(demultiplexer_1_out4[0]),
    .b2_short(demultiplexer_1_out4[2]), .b2_long(demultiplexer_1_out4[3]), .clk_100th(clock_1_out),
    .reset(DipSwitch_1_sw10), .x7_2(state4_countdown_1_x7_2), .x7_3(state4_countdown_1_x7_3),
    .x7_4(state4_countdown_1_x7_4), .x7_5(state4_countdown_1_x7_5), .x7_6(state4_countdown_1_x7_6),
    .x7_7(state4_countdown_1_x7_7));
  state2_alarmclock state2_alarmclock_1 (
    .alarm(alarm_clock_interrupter_1_alarm), .b1_short(demultiplexer_1_out2[0]),
    .b1_long(demultiplexer_1_out2[1]), .b2_short(demultiplexer_1_out2[2]), .clk_100th(clock_1_out),
    .b2_long(demultiplexer_1_out2[3]), .dip_switch(DipSwitch_1_sw1), .reset(DipSwitch_1_sw10),
    .x7_m1(state2_alarmclock_1_x7_m1), .x7_m2(state2_alarmclock_1_x7_m2), .x7_h1(state2_alarmclock_1_x7_h1),
    .x7_h2(state2_alarmclock_1_x7_h2), .x7_6(state2_alarmclock_1_x7_6), .x7_7(state2_alarmclock_1_x7_7),
    .alarm_on(state2_alarmclock_1_alarm_on), .high(high_buzzer_1));
  state3_stopwatch state3_stopwatch_1 (
    .b1_short(demultiplexer_1_out3[0]), .b2_short(demultiplexer_1_out3[2]), .dipswitch_1(DipSwitch_1_sw1),
    .clk_100th(clock_1_out), .reset(DipSwitch_1_sw10), .x7_0(state3_stopwatch_1_x7_0),
    .x7_1(state3_stopwatch_1_x7_1), .x7_2(state3_stopwatch_1_x7_2), .x7_3(state3_stopwatch_1_x7_3),
    .x7_4(state3_stopwatch_1_x7_4), .x7_5(state3_stopwatch_1_x7_5));
  Multiplexer #(.select(3), .width(7), .enable("false")) multiplexer_1 (
    .in0(clock24h_display_1_x7_7), .in1(state1_timezone_1_x7_7), .in2(state2_alarmclock_1_x7_7),
    .in3(state3_stopwatch_1_x7_5), .in4(state4_countdown_1_x7_7), .out(multiplexer_1_out),
    .sel(main_statemachine_1_state_binary));  // open: in5, in6, in7
  state5_game state5_game_1 (
    .reset(DipSwitch_1_sw10), .b1_short(demultiplexer_1_out5[0]), .b2_short(demultiplexer_1_out5[2]),
    .b1_long(demultiplexer_1_out5[1]), .ds1(DipSwitch_1_sw1), .clk(clock_1_out),
    .Output_bus_1(state5_game_1_output_bus_1), .Output_bus_2(state5_game_1_output_bus_2),
    .Output_bus_3(state5_game_1_output_bus_3), .Output_bus_4(state5_game_1_output_bus_4),
    .led(state5_game_1_led));
  _7_Segment_Display L_7_Segment_Display_1 (
    .g(multiplexer_1_out[6]), .f(multiplexer_1_out[5]), .a(multiplexer_1_out[0]), .b(multiplexer_1_out[1]),
    .e(multiplexer_1_out[4]), .d(multiplexer_1_out[3]), .c(multiplexer_1_out[2]));  // open: dp
  Decoder #(.select(3)) decoder_1 (
    .out0(decoder_1_out0), .out1(decoder_1_out1), .out2(decoder_1_out2), .out3(decoder_1_out3),
    .out4(decoder_1_out4), .out5(decoder_1_out5), .out6(decoder_1_out6),
    .sel(main_statemachine_1_state_binary), .en(1'b1));  // open: out7
  LED LED_3 (.in(decoder_1_out2));
  LED LED_4 (.in(decoder_1_out3));
  LED LED_1 (.in(decoder_1_out0));
  LED LED_2 (.in(decoder_1_out1));
  LED LED_6 (.in(decoder_1_out5));
  LED LED_5 (.in(decoder_1_out4));
  LED LED_7 (.in(decoder_1_out6));
  Multiplexer #(.select(3), .width(7), .enable("false")) multiplexer_2 (
    .in0(clock24h_display_1_x7_6), .in1(state1_timezone_1_x7_6), .in2(state2_alarmclock_1_x7_6),
    .in3(state3_stopwatch_1_x7_4), .in4(state4_countdown_1_x7_6), .in6(state6_piano_1_x7_4),
    .out(multiplexer_2_out), .sel(main_statemachine_1_state_binary));  // open: in5, in7
  _7_Segment_Display L_7_Segment_Display_2 (
    .g(multiplexer_2_out[6]), .f(multiplexer_2_out[5]), .a(multiplexer_2_out[0]), .b(multiplexer_2_out[1]),
    .e(multiplexer_2_out[4]), .d(multiplexer_2_out[3]), .c(multiplexer_2_out[2]));  // open: dp
  Multiplexer #(.select(3), .width(7), .enable("false")) multiplexer_3 (
    .in0(clock24h_display_1_x7_5), .in1(state1_timezone_1_x7_5), .in2(state2_alarmclock_1_x7_h2),
    .in3(state3_stopwatch_1_x7_3), .in4(state4_countdown_1_x7_5), .in5(state5_game_1_output_bus_4),
    .in6(state6_piano_1_x7_3), .out(multiplexer_3_out), .sel(main_statemachine_1_state_binary));  // open: in7
  _7_Segment_Display L_7_Segment_Display_3 (
    .g(multiplexer_3_out[6]), .f(multiplexer_3_out[5]), .a(multiplexer_3_out[0]), .b(multiplexer_3_out[1]),
    .e(multiplexer_3_out[4]), .d(multiplexer_3_out[3]), .c(multiplexer_3_out[2]));  // open: dp
  LED Game_LED (.in(state5_game_1_led));
  Multiplexer #(.select(3), .width(7), .enable("false")) multiplexer_4 (
    .in0(clock24h_display_1_x7_4), .in1({7{1'b0}}), .in2(state2_alarmclock_1_x7_h1),
    .in3(state3_stopwatch_1_x7_2), .in4(state4_countdown_1_x7_4), .in5(state5_game_1_output_bus_3),
    .in6(state6_piano_1_x7_2), .out(multiplexer_4_out), .sel(main_statemachine_1_state_binary));  // open: in7
  _7_Segment_Display L_7_Segment_Display_4 (
    .g(multiplexer_4_out[6]), .f(multiplexer_4_out[5]), .a(multiplexer_4_out[0]), .b(multiplexer_4_out[1]),
    .e(multiplexer_4_out[4]), .d(multiplexer_4_out[3]), .c(multiplexer_4_out[2]));  // open: dp
  Multiplexer #(.select(3), .width(7), .enable("false")) multiplexer_5 (
    .in0(clock24h_display_1_x7_3), .in1(state1_timezone_1_x7_3), .in2(state2_alarmclock_1_x7_m2),
    .in3(state3_stopwatch_1_x7_1), .in4(state4_countdown_1_x7_3), .in5(state5_game_1_output_bus_2),
    .in6(state6_piano_1_x7_1), .out(multiplexer_5_out), .sel(main_statemachine_1_state_binary));  // open: in7
  _7_Segment_Display L_7_Segment_Display_5 (
    .g(multiplexer_5_out[6]), .f(multiplexer_5_out[5]), .a(multiplexer_5_out[0]), .b(multiplexer_5_out[1]),
    .e(multiplexer_5_out[4]), .d(multiplexer_5_out[3]), .c(multiplexer_5_out[2]));  // open: dp
  Multiplexer #(.select(3), .width(7), .enable("false")) multiplexer_6 (
    .in0(clock24h_display_1_x7_2), .in1(state1_timezone_1_x7_2), .in2(state2_alarmclock_1_x7_m1),
    .in3(state3_stopwatch_1_x7_0), .in4(state4_countdown_1_x7_2), .in5(state5_game_1_output_bus_1),
    .in6(state6_piano_1_x7_0), .out(multiplexer_6_out), .sel(main_statemachine_1_state_binary));  // open: in7
  _7_Segment_Display L_7_Segment_Display_6 (
    .g(multiplexer_6_out[6]), .f(multiplexer_6_out[5]), .a(multiplexer_6_out[0]), .b(multiplexer_6_out[1]),
    .e(multiplexer_6_out[4]), .d(multiplexer_6_out[3]), .c(multiplexer_6_out[2]));  // open: dp
  and and_1 (and_1_out, state2_alarmclock_1_alarm_on, ~or_1_out);  // AND_Gate
  or or_1 (or_1_out, state1_timezone_1_set_on, clock24h_display_1_set_on);
  time_comparator alarm_clock_interrupter_1 (
    .alarm_s1(7'b0111111), .alarm_s2(7'b0111111), .alarm_m1(state2_alarmclock_1_x7_m1),
    .alarm_m2(state2_alarmclock_1_x7_m2), .alarm_h1(state2_alarmclock_1_x7_h1),
    .alarm_h2(state2_alarmclock_1_x7_h2), .clock_s1(clock24h_display_1_x7_2),
    .clock_s2(clock24h_display_1_x7_3), .clock_m1(clock24h_display_1_x7_4),
    .clock_m2(clock24h_display_1_x7_5), .clock_h1(clock24h_display_1_x7_6),
    .clock_h2(clock24h_display_1_x7_7), .alarm_on(and_1_out), .alarm(alarm_clock_interrupter_1_alarm));

  assign gnd_buzzer1 = 1'b0;
  assign gnd_buzzer_2 = 1'b0;
  assign gnd_buzzer_3 = 1'b0;

  // Notes on the sheet:
  //   current state
  //   Place those LEDs such that they are on top of the dipswitches as they indicate the state
  //   place this led the most right
  //   Keep those displays in order as they display the time
  //   Connect those pins such that the 3 buzzers are connected. Buzzer 1&2 are for the piano, buzzer 3 for the alarm
endmodule

module main_statemachine (
  input  reset,
  input  alarm,
  input  button1_short,
  input  button2_short,
  input  dippswitch1,
  input  clk,
  output [2:0] state_binary
);

  wire main_statemachine_logic_1_nextstate_bit0, main_statemachine_logic_1_nextstate_bit1,
       main_statemachine_logic_1_nextstate_bit2, or_1_out, or_2_out;

  main_statemachine_logic main_statemachine_logic_1 (
    .state_bit2(state_binary[2]), .state_bit1(state_binary[1]), .state_bit0(state_binary[0]),
    .button1_short(button1_short), .button2_short(button2_short), .Dipswitch1(dippswitch1),
    .nextstate_bit2(main_statemachine_logic_1_nextstate_bit2),
    .nextstate_bit1(main_statemachine_logic_1_nextstate_bit1),
    .nextstate_bit0(main_statemachine_logic_1_nextstate_bit0));
  D_Flip_Flop d_ff_1 (
    .D(main_statemachine_logic_1_nextstate_bit2), .clk(clk), .Q(state_binary[2]), .reset(or_1_out));  // open: Qn, preset
  D_Flip_Flop d_ff_2 (
    .D(main_statemachine_logic_1_nextstate_bit1), .clk(clk), .Q(state_binary[1]), .preset(alarm),
    .reset(reset));  // open: Qn
  D_Flip_Flop d_ff_3 (
    .D(main_statemachine_logic_1_nextstate_bit0), .clk(clk), .Q(state_binary[0]), .reset(or_2_out));  // open: Qn, preset
  or or_1 (or_1_out, alarm, reset);
  or or_2 (or_2_out, alarm, reset);

  // Notes on the sheet:
  //   if alarm on: set state 010
endmodule

module main_statemachine_logic (
  input  state_bit2,
  input  state_bit1,
  input  state_bit0,
  input  button1_short,
  input  button2_short,
  input  Dipswitch1,
  output nextstate_bit2,
  output nextstate_bit1,
  output nextstate_bit0
);

  wire and_1_out, and_2_out, and_3_out, and_4_out, and_5_out, and_6_out, and_7_out, and_8_out, and_9_out,
       and_10_out, and_11_out, and_12_out, and_13_out, and_14_out, and_15_out, and_16_out, and_17_out,
       and_18_out, and_19_out, and_20_out, not_1_out, not_2_out, not_3_out, not_4_out, not_5_out, not_6_out,
       not_7_out, not_8_out, not_9_out, not_10_out, not_11_out, not_12_out, not_13_out, not_14_out,
       not_15_out, not_16_out, not_17_out, not_18_out, not_19_out, not_20_out, not_21_out, not_22_out,
       not_23_out, not_24_out, not_25_out, not_26_out, not_27_out, not_28_out, not_29_out, not_30_out,
       not_31_out, not_32_out, not_33_out;

  not not_1 (not_1_out, state_bit2);
  not not_2 (not_2_out, state_bit1);
  not not_3 (not_3_out, state_bit0);
  not not_4 (not_4_out, button2_short);
  not not_5 (not_5_out, button1_short);
  not not_6 (not_6_out, state_bit1);
  not not_7 (not_7_out, button1_short);
  not not_8 (not_8_out, Dipswitch1);
  not not_9 (not_9_out, state_bit1);
  not not_10 (not_10_out, button2_short);
  not not_11 (not_11_out, state_bit1);
  not not_12 (not_12_out, state_bit0);
  not not_13 (not_13_out, button2_short);
  not not_14 (not_14_out, state_bit1);
  not not_15 (not_15_out, button1_short);
  not not_16 (not_16_out, button1_short);
  not not_17 (not_17_out, button2_short);
  not not_18 (not_18_out, Dipswitch1);
  not not_19 (not_19_out, state_bit2);
  not not_20 (not_20_out, state_bit0);
  not not_21 (not_21_out, state_bit2);
  not not_22 (not_22_out, state_bit0);
  not not_23 (not_23_out, button1_short);
  not not_24 (not_24_out, state_bit1);
  not not_25 (not_25_out, state_bit0);
  not not_26 (not_26_out, button1_short);
  not not_27 (not_27_out, button1_short);
  not not_28 (not_28_out, button2_short);
  not not_29 (not_29_out, Dipswitch1);
  not not_30 (not_30_out, state_bit0);
  not not_31 (not_31_out, button2_short);
  not not_32 (not_32_out, state_bit0);
  not not_33 (not_33_out, button2_short);
  and and_1 (and_1_out, not_1_out, not_2_out, not_3_out, button1_short, not_4_out, Dipswitch1);
  and and_2 (and_2_out, state_bit1, state_bit0, not_5_out, button2_short, Dipswitch1);
  and and_3 (and_3_out, state_bit2, not_6_out, not_7_out);
  and and_4 (and_4_out, state_bit2, not_8_out);
  and and_5 (and_5_out, state_bit2, not_9_out, button2_short);
  and and_6 (and_6_out, state_bit2, state_bit0);
  and and_7 (and_7_out, state_bit2, state_bit1, not_10_out);
  and and_8 (and_8_out, not_11_out, not_12_out, button1_short, not_13_out, Dipswitch1);
  and and_9 (and_9_out, not_14_out, state_bit0, not_15_out, button2_short, Dipswitch1);
  and and_10 (and_10_out, state_bit1, not_16_out, not_17_out);
  and and_11 (and_11_out, state_bit1, not_18_out);
  and and_12 (and_12_out, not_19_out, state_bit1, not_20_out, button2_short);
  and and_13 (and_13_out, state_bit1, state_bit0, button1_short);
  and and_14 (and_14_out, not_21_out, not_22_out, not_23_out, button2_short, Dipswitch1);
  and and_15 (and_15_out, not_24_out, not_25_out, not_26_out, button2_short, Dipswitch1);
  and and_16 (and_16_out, state_bit0, not_27_out, not_28_out);
  and and_17 (and_17_out, state_bit0, not_29_out);
  and and_18 (and_18_out, state_bit0, button1_short, button2_short);
  and and_19 (and_19_out, state_bit1, not_30_out, button1_short, not_31_out, Dipswitch1);
  and and_20 (and_20_out, state_bit2, not_32_out, button1_short, not_33_out, Dipswitch1);
  or or_1 (nextstate_bit2, and_1_out, and_2_out, and_3_out, and_4_out, and_5_out, and_6_out, and_7_out);
  or or_2 (nextstate_bit1, and_8_out, and_9_out, and_10_out, and_11_out, and_12_out, and_13_out);
  or or_3 (nextstate_bit0, and_14_out, and_15_out, and_16_out, and_17_out, and_18_out, and_19_out, and_20_out);
endmodule

module input_ctrl (
  input  button,
  input  clk,
  output short,
  output long
);

  wire and_1_out, and_2_out, d_ff_1_q, d_ff_2_q, not_1_out, not_2_out, not_3_out;
  wire [7:0] counter_1_q;

  not not_1 (not_1_out, button);
  not not_2 (not_2_out, button);
  D_Flip_Flop d_ff_1 (.D(button), .clk(clk), .Q(d_ff_1_q), .reset(long));  // open: Qn, preset
  Counter counter_1 (
    .clr(not_2_out), .load(and_2_out), .up(1'b1), .clk(clk), .D(counter_1_q), .Q(counter_1_q));  // open: count, carry
  and and_1 (and_1_out, not_1_out, d_ff_1_q);
  D_Flip_Flop d_ff_2 (.D(and_1_out), .clk(clk), .Q(d_ff_2_q), .reset(long));  // open: Qn, preset
  and and_2 (and_2_out, counter_1_q[5], counter_1_q[6]);
  not not_3 (not_3_out, and_2_out);
  D_Flip_Flop d_ff_3 (.D(and_2_out), .clk(clk), .Q(long));  // open: Qn, preset, reset
  and and_3 (short, d_ff_2_q, not_3_out);

  // Notes on the sheet:
  //   Signal at the end when the button is released
  //   Duration of  "long" : ~1s
endmodule

module clock24h (
  input  reset,
  input  b1_long,
  input  dip_switch,
  input  clk100ths,
  input  b1_short,
  input  b2_short,
  input  pause,
  input  [1:0] timezone,
  input  countdown,
  output b00,
  output b01,
  output b02,
  output b03,
  output b10,
  output b11,
  output b12,
  output b13,
  output b20,
  output b21,
  output b22,
  output b23,
  output b30,
  output b31,
  output b32,
  output b40,
  output b41,
  output b42,
  output b43,
  output b50,
  output b51,
  output b52,
  output b60,
  output b61,
  output b62,
  output b63,
  output b70,
  output b71,
  output set_on,
  output [2:0] set_status
);

  wire and_1_out, and_2_out, counter24_1_e0, counter24_1_e1, counter24_1_e2, counter24_1_e3, counter24_1_z0,
       counter24_1_z1, counter_0to5_1_b0, counter_0to5_1_b1, counter_0to5_1_b2, counter_0to5_2_b0,
       counter_0to5_2_b1, counter_0to5_2_b2, counter_0to5_2_n_out, counter_0to5_3_b0, counter_0to5_3_b1,
       counter_0to5_3_b2, counter_0to5_3_n_out, counter_0to9_1_b0, counter_0to9_1_b1, counter_0to9_1_b2,
       counter_0to9_1_b3, counter_0to9_1_n_out, counter_0to9_2_b0, counter_0to9_2_b1, counter_0to9_2_b2,
       counter_0to9_2_b3, counter_0to9_2_n_out, counter_0to9_3_b0, counter_0to9_3_b1, counter_0to9_3_b2,
       counter_0to9_3_b3, counter_0to9_3_n_out, counter_0to9_4_b0, counter_0to9_4_b1, counter_0to9_4_b2,
       counter_0to9_4_b3, counter_0to9_4_n_out, d_ff_4_q, d_ff_4_qn, d_ff_9_q, d_ff_14_q, d_ff_19_q,
       d_ff_23_q, d_ff_28_q, d_ff_32_q, d_ff_33_q, d_ff_34_q, d_ff_35_q, d_ff_36_q, d_ff_37_q, d_ff_38_q,
       demultiplexer_1_out0, demultiplexer_1_out1, demultiplexer_1_out2, demultiplexer_1_out3,
       demultiplexer_1_out4, demultiplexer_1_out5, multiplexer_1_out, multiplexer_2_out, multiplexer_3_out,
       multiplexer_4_out, multiplexer_5_out, not_1_out, or_1_out, or_2_out, or_3_out, or_4_out, or_5_out,
       or_6_out, or_7_out, or_8_out, set_h, set_m0, set_m1, set_s0, set_s1;

  and and_1 (and_1_out, b1_long, ~dip_switch);  // AND_Gate
  S_R_Flip_Flop s_r_ff_1 (
    .S(and_1_out), .R(1'b0), .clk(clk100ths), .Q(set_on), .reset(demultiplexer_1_out5));  // open: Qn, preset
  counter_0to5 counter_0to5_1 (
    .a2(set_status[2]), .a1(set_status[1]), .a0(set_status[0]), .n(b2_short), .countdown(1'b0),
    .b2(counter_0to5_1_b2), .b1(counter_0to5_1_b1), .b0(counter_0to5_1_b0));  // open: n_out
  D_Flip_Flop d_ff_1 (.D(counter_0to5_1_b2), .clk(clk100ths), .Q(set_status[2]), .reset(or_1_out));  // open: Qn, preset
  D_Flip_Flop d_ff_2 (.D(counter_0to5_1_b1), .clk(clk100ths), .Q(set_status[1]), .reset(or_1_out));  // open: Qn, preset
  D_Flip_Flop d_ff_3 (.D(counter_0to5_1_b0), .clk(clk100ths), .Q(set_status[0]), .reset(or_1_out));  // open: Qn, preset
  not not_1 (not_1_out, set_on);
  or or_1 (or_1_out, reset, not_1_out);
  and and_2 (and_2_out, ~set_on, countdown);  // AND_Gate
  D_Flip_Flop d_ff_4 (.D(d_ff_4_qn), .clk(clk100ths), .Q(d_ff_4_q), .Qn(d_ff_4_qn), .reset(or_2_out));  // open: preset
  or or_2 (or_2_out, set_on, pause);
  and and_3 (set_s0, demultiplexer_1_out0, b1_short);
  counter_0to9 counter_0to9_1 (
    .a3(b03), .a2(b02), .a1(b01), .a0(b00), .n(d_ff_4_q), .countdown(and_2_out), .b3(counter_0to9_1_b3),
    .b2(counter_0to9_1_b2), .b1(counter_0to9_1_b1), .b0(counter_0to9_1_b0), .n_out(counter_0to9_1_n_out));
  Demultiplexer #(.select(3), .enable("false")) demultiplexer_1 (
    .out0(demultiplexer_1_out0), .out1(demultiplexer_1_out1), .out2(demultiplexer_1_out2),
    .out3(demultiplexer_1_out3), .out4(demultiplexer_1_out4), .out5(demultiplexer_1_out5), .in(1'b1),
    .sel(set_status));  // open: out6, out7
  and and_4 (set_s1, demultiplexer_1_out1, b1_short);
  and and_5 (set_m0, demultiplexer_1_out2, b1_short);
  D_Flip_Flop d_ff_5 (.D(counter_0to9_1_b3), .clk(clk100ths), .Q(b03), .reset(reset));  // open: Qn, preset
  D_Flip_Flop d_ff_6 (.D(counter_0to9_1_b2), .clk(clk100ths), .Q(b02), .reset(reset));  // open: Qn, preset
  D_Flip_Flop d_ff_7 (.D(counter_0to9_1_b1), .clk(clk100ths), .Q(b01), .reset(reset));  // open: Qn, preset
  D_Flip_Flop d_ff_8 (.D(counter_0to9_1_b0), .clk(clk100ths), .Q(b00), .reset(reset));  // open: Qn, preset
  D_Flip_Flop d_ff_9 (.D(counter_0to9_1_n_out), .clk(clk100ths), .Q(d_ff_9_q), .reset(or_3_out));  // open: Qn, preset
  and and_6 (set_m1, demultiplexer_1_out3, b1_short);
  and and_7 (set_h, demultiplexer_1_out4, b1_short);
  or or_3 (or_3_out, set_on, reset);
  counter_0to9 counter_0to9_2 (
    .a3(b13), .a2(b12), .a1(b11), .a0(b10), .n(d_ff_9_q), .countdown(and_2_out), .b3(counter_0to9_2_b3),
    .b2(counter_0to9_2_b2), .b1(counter_0to9_2_b1), .b0(counter_0to9_2_b0), .n_out(counter_0to9_2_n_out));
  D_Flip_Flop d_ff_10 (.D(counter_0to9_2_b3), .clk(clk100ths), .Q(b13), .reset(reset));  // open: Qn, preset
  D_Flip_Flop d_ff_11 (.D(counter_0to9_2_b2), .clk(clk100ths), .Q(b12), .reset(reset));  // open: Qn, preset
  D_Flip_Flop d_ff_12 (.D(counter_0to9_2_b1), .clk(clk100ths), .Q(b11), .reset(reset));  // open: Qn, preset
  D_Flip_Flop d_ff_13 (.D(counter_0to9_2_b0), .clk(clk100ths), .Q(b10), .reset(reset));  // open: Qn, preset
  D_Flip_Flop d_ff_14 (.D(counter_0to9_2_n_out), .clk(clk100ths), .Q(d_ff_14_q), .reset(or_4_out));  // open: Qn, preset
  or or_4 (or_4_out, set_on, reset);
  Multiplexer #(.enable("false")) multiplexer_1 (.in0(d_ff_14_q), .in1(set_s0), .out(multiplexer_1_out), .sel(set_on));
  counter_0to9 counter_0to9_3 (
    .a3(b23), .a2(b22), .a1(b21), .a0(b20), .n(multiplexer_1_out), .countdown(and_2_out),
    .b3(counter_0to9_3_b3), .b2(counter_0to9_3_b2), .b1(counter_0to9_3_b1), .b0(counter_0to9_3_b0),
    .n_out(counter_0to9_3_n_out));
  D_Flip_Flop d_ff_15 (.D(counter_0to9_3_b3), .clk(clk100ths), .Q(b23), .reset(reset));  // open: Qn, preset
  D_Flip_Flop d_ff_16 (.D(counter_0to9_3_b2), .clk(clk100ths), .Q(b22), .reset(reset));  // open: Qn, preset
  D_Flip_Flop d_ff_17 (.D(counter_0to9_3_b1), .clk(clk100ths), .Q(b21), .reset(reset));  // open: Qn, preset
  D_Flip_Flop d_ff_18 (.D(counter_0to9_3_b0), .clk(clk100ths), .Q(b20), .reset(reset));  // open: Qn, preset
  D_Flip_Flop d_ff_19 (.D(counter_0to9_3_n_out), .clk(clk100ths), .Q(d_ff_19_q), .reset(or_5_out));  // open: Qn, preset
  or or_5 (or_5_out, set_on, reset);
  Multiplexer #(.enable("false")) multiplexer_2 (.in0(d_ff_19_q), .in1(set_s1), .out(multiplexer_2_out), .sel(set_on));
  counter_0to5 counter_0to5_2 (
    .a2(b32), .a1(b31), .a0(b30), .n(multiplexer_2_out), .countdown(and_2_out), .b2(counter_0to5_2_b2),
    .b1(counter_0to5_2_b1), .b0(counter_0to5_2_b0), .n_out(counter_0to5_2_n_out));
  D_Flip_Flop d_ff_20 (.D(counter_0to5_2_b2), .clk(clk100ths), .Q(b32), .reset(reset));  // open: Qn, preset
  D_Flip_Flop d_ff_21 (.D(counter_0to5_2_b1), .clk(clk100ths), .Q(b31), .reset(reset));  // open: Qn, preset
  D_Flip_Flop d_ff_22 (.D(counter_0to5_2_b0), .clk(clk100ths), .Q(b30), .reset(reset));  // open: Qn, preset
  D_Flip_Flop d_ff_23 (.D(counter_0to5_2_n_out), .clk(clk100ths), .Q(d_ff_23_q), .reset(or_6_out));  // open: Qn, preset
  or or_6 (or_6_out, set_on, reset);
  Multiplexer #(.enable("false")) multiplexer_3 (.in0(d_ff_23_q), .in1(set_m0), .out(multiplexer_3_out), .sel(set_on));
  counter_0to9 counter_0to9_4 (
    .a3(b43), .a2(b42), .a1(b41), .a0(b40), .n(multiplexer_3_out), .countdown(and_2_out),
    .b3(counter_0to9_4_b3), .b2(counter_0to9_4_b2), .b1(counter_0to9_4_b1), .b0(counter_0to9_4_b0),
    .n_out(counter_0to9_4_n_out));
  D_Flip_Flop d_ff_24 (.D(counter_0to9_4_b3), .clk(clk100ths), .Q(b43), .reset(reset));  // open: Qn, preset
  D_Flip_Flop d_ff_25 (.D(counter_0to9_4_b2), .clk(clk100ths), .Q(b42), .reset(reset));  // open: Qn, preset
  D_Flip_Flop d_ff_26 (.D(counter_0to9_4_b1), .clk(clk100ths), .Q(b41), .reset(reset));  // open: Qn, preset
  D_Flip_Flop d_ff_27 (.D(counter_0to9_4_b0), .clk(clk100ths), .Q(b40), .reset(reset));  // open: Qn, preset
  D_Flip_Flop d_ff_28 (.D(counter_0to9_4_n_out), .clk(clk100ths), .Q(d_ff_28_q), .reset(or_7_out));  // open: Qn, preset
  or or_7 (or_7_out, set_on, reset);
  Multiplexer #(.enable("false")) multiplexer_4 (.in0(d_ff_28_q), .in1(set_m1), .out(multiplexer_4_out), .sel(set_on));
  counter_0to5 counter_0to5_3 (
    .a2(b52), .a1(b51), .a0(b50), .n(multiplexer_4_out), .countdown(and_2_out), .b2(counter_0to5_3_b2),
    .b1(counter_0to5_3_b1), .b0(counter_0to5_3_b0), .n_out(counter_0to5_3_n_out));
  D_Flip_Flop d_ff_29 (.D(counter_0to5_3_b2), .clk(clk100ths), .Q(b52), .reset(reset));  // open: Qn, preset
  D_Flip_Flop d_ff_30 (.D(counter_0to5_3_b1), .clk(clk100ths), .Q(b51), .reset(reset));  // open: Qn, preset
  D_Flip_Flop d_ff_31 (.D(counter_0to5_3_b0), .clk(clk100ths), .Q(b50), .reset(reset));  // open: Qn, preset
  D_Flip_Flop d_ff_32 (.D(counter_0to5_3_n_out), .clk(clk100ths), .Q(d_ff_32_q), .reset(or_8_out));  // open: Qn, preset
  or or_8 (or_8_out, set_on, reset);
  Multiplexer #(.enable("false")) multiplexer_5 (.in0(d_ff_32_q), .in1(set_h), .out(multiplexer_5_out), .sel(set_on));
  counter24 counter24_1 (
    .z1_in(d_ff_33_q), .z0_in(d_ff_34_q), .b3(d_ff_35_q), .b2(d_ff_36_q), .b1(d_ff_37_q), .b0(d_ff_38_q),
    .countdown(and_2_out), .n(multiplexer_5_out), .z1(counter24_1_z1), .z0(counter24_1_z0),
    .e3(counter24_1_e3), .e2(counter24_1_e2), .e1(counter24_1_e1), .e0(counter24_1_e0));
  D_Flip_Flop d_ff_33 (.D(counter24_1_z1), .clk(clk100ths), .Q(d_ff_33_q), .reset(reset));  // open: Qn, preset
  D_Flip_Flop d_ff_34 (.D(counter24_1_z0), .clk(clk100ths), .Q(d_ff_34_q), .reset(reset));  // open: Qn, preset
  D_Flip_Flop d_ff_35 (.D(counter24_1_e3), .clk(clk100ths), .Q(d_ff_35_q), .reset(reset));  // open: Qn, preset
  D_Flip_Flop d_ff_36 (.D(counter24_1_e2), .clk(clk100ths), .Q(d_ff_36_q), .reset(reset));  // open: Qn, preset
  D_Flip_Flop d_ff_37 (.D(counter24_1_e1), .clk(clk100ths), .Q(d_ff_37_q), .reset(reset));  // open: Qn, preset
  D_Flip_Flop d_ff_38 (.D(counter24_1_e0), .clk(clk100ths), .Q(d_ff_38_q), .reset(reset));  // open: Qn, preset
  timezone_adder timezone_adder_1 (
    .b60(d_ff_38_q), .b61(d_ff_37_q), .b62(d_ff_36_q), .b63(d_ff_35_q), .b70(d_ff_34_q), .b71(d_ff_33_q),
    .timezone(timezone), .b60_out(b60), .b61_out(b61), .b62_out(b62), .b63_out(b63), .b70_out(b70),
    .b71_out(b71));

  // Other names for the same wires on the sheet: clk_100ths = clk100ths

  // Notes on the sheet:
  //   set-mode is active
endmodule

module clock24h_display (
  input  reset,
  input  b1_long,
  input  dip_switch,
  input  clk_100ths,
  input  b1_short,
  input  b2_short,
  input  [1:0] timezone,
  input  pause,
  input  countdown,
  output [6:0] x7_0,
  output [6:0] x7_1,
  output [6:0] x7_2,
  output [6:0] x7_3,
  output [6:0] x7_4,
  output [6:0] x7_5,
  output [6:0] x7_6,
  output [6:0] x7_7,
  output set_on
);

  wire clock24h_1_b00, clock24h_1_b01, clock24h_1_b02, clock24h_1_b03, clock24h_1_b10, clock24h_1_b11,
       clock24h_1_b12, clock24h_1_b13, clock24h_1_b20, clock24h_1_b21, clock24h_1_b22, clock24h_1_b23,
       clock24h_1_b30, clock24h_1_b31, clock24h_1_b32, clock24h_1_b40, clock24h_1_b41, clock24h_1_b42,
       clock24h_1_b43, clock24h_1_b50, clock24h_1_b51, clock24h_1_b52, clock24h_1_b60, clock24h_1_b61,
       clock24h_1_b62, clock24h_1_b63, clock24h_1_b70, clock24h_1_b71, demultiplexer_1_out0,
       demultiplexer_1_out1, demultiplexer_1_out2, demultiplexer_1_out3, demultiplexer_1_out4, not_1_out;
  wire [2:0] clock24h_1_set_status;
  wire [6:0] bin2display_3_a, bin2display_4_a, bin2display_5_a, bin2display_6_a, bin2display_7_a,
       bin2display_8_a;
  wire [7:0] counter_1_q;

  clock24h clock24h_1 (
    .reset(reset), .b1_long(b1_long), .dip_switch(dip_switch), .clk100ths(clk_100ths), .b1_short(b1_short),
    .b2_short(b2_short), .pause(pause), .timezone(timezone), .countdown(countdown), .b00(clock24h_1_b00),
    .b01(clock24h_1_b01), .b02(clock24h_1_b02), .b03(clock24h_1_b03), .b10(clock24h_1_b10),
    .b11(clock24h_1_b11), .b12(clock24h_1_b12), .b13(clock24h_1_b13), .b20(clock24h_1_b20),
    .b21(clock24h_1_b21), .b22(clock24h_1_b22), .b23(clock24h_1_b23), .b30(clock24h_1_b30),
    .b31(clock24h_1_b31), .b32(clock24h_1_b32), .b40(clock24h_1_b40), .b41(clock24h_1_b41),
    .b42(clock24h_1_b42), .b43(clock24h_1_b43), .b50(clock24h_1_b50), .b51(clock24h_1_b51),
    .b52(clock24h_1_b52), .b60(clock24h_1_b60), .b61(clock24h_1_b61), .b62(clock24h_1_b62),
    .b63(clock24h_1_b63), .b70(clock24h_1_b70), .b71(clock24h_1_b71), .set_on(set_on),
    .set_status(clock24h_1_set_status));
  binary_to_display_code bin2display_8 (
    .b0(clock24h_1_b70), .b1(clock24h_1_b71), .b2(1'b0), .b3(1'b0), .a(bin2display_8_a[0]),
    .b(bin2display_8_a[1]), .c(bin2display_8_a[2]), .d(bin2display_8_a[3]), .e(bin2display_8_a[4]),
    .f(bin2display_8_a[5]), .g(bin2display_8_a[6]));
  binary_to_display_code bin2display_7 (
    .b0(clock24h_1_b60), .b1(clock24h_1_b61), .b2(clock24h_1_b62), .b3(clock24h_1_b63),
    .a(bin2display_7_a[0]), .b(bin2display_7_a[1]), .c(bin2display_7_a[2]), .d(bin2display_7_a[3]),
    .e(bin2display_7_a[4]), .f(bin2display_7_a[5]), .g(bin2display_7_a[6]));
  binary_to_display_code bin2display_6 (
    .b0(clock24h_1_b50), .b1(clock24h_1_b51), .b2(clock24h_1_b52), .b3(1'b0), .a(bin2display_6_a[0]),
    .b(bin2display_6_a[1]), .c(bin2display_6_a[2]), .d(bin2display_6_a[3]), .e(bin2display_6_a[4]),
    .f(bin2display_6_a[5]), .g(bin2display_6_a[6]));
  binary_to_display_code bin2display_5 (
    .b0(clock24h_1_b40), .b1(clock24h_1_b41), .b2(clock24h_1_b42), .b3(clock24h_1_b43),
    .a(bin2display_5_a[0]), .b(bin2display_5_a[1]), .c(bin2display_5_a[2]), .d(bin2display_5_a[3]),
    .e(bin2display_5_a[4]), .f(bin2display_5_a[5]), .g(bin2display_5_a[6]));
  binary_to_display_code bin2display_4 (
    .b0(clock24h_1_b30), .b1(clock24h_1_b31), .b2(clock24h_1_b32), .b3(1'b0), .a(bin2display_4_a[0]),
    .b(bin2display_4_a[1]), .c(bin2display_4_a[2]), .d(bin2display_4_a[3]), .e(bin2display_4_a[4]),
    .f(bin2display_4_a[5]), .g(bin2display_4_a[6]));
  Counter counter_1 (
    .clr(not_1_out), .load(1'b0), .up(1'b1), .clk(clk_100ths), .Q(counter_1_q));  // open: count, D, carry
  not not_1 (not_1_out, set_on);
  binary_to_display_code bin2display_3 (
    .b0(clock24h_1_b20), .b1(clock24h_1_b21), .b2(clock24h_1_b22), .b3(clock24h_1_b23),
    .a(bin2display_3_a[0]), .b(bin2display_3_a[1]), .c(bin2display_3_a[2]), .d(bin2display_3_a[3]),
    .e(bin2display_3_a[4]), .f(bin2display_3_a[5]), .g(bin2display_3_a[6]));
  binary_to_display_code bin2display_2 (
    .b0(clock24h_1_b10), .b1(clock24h_1_b11), .b2(clock24h_1_b12), .b3(clock24h_1_b13), .a(x7_1[0]),
    .b(x7_1[1]), .c(x7_1[2]), .d(x7_1[3]), .e(x7_1[4]), .f(x7_1[5]), .g(x7_1[6]));
  Multiplexer #(.width(7), .enable("false")) multiplexer_1 (
    .in0(bin2display_3_a), .in1({7{1'b0}}), .out(x7_2), .sel(demultiplexer_1_out0));
  Multiplexer #(.width(7), .enable("false")) multiplexer_2 (
    .in0(bin2display_4_a), .in1({7{1'b0}}), .out(x7_3), .sel(demultiplexer_1_out1));
  Multiplexer #(.width(7), .enable("false")) multiplexer_3 (
    .in0(bin2display_5_a), .in1({7{1'b0}}), .out(x7_4), .sel(demultiplexer_1_out2));
  Multiplexer #(.width(7), .enable("false")) multiplexer_4 (
    .in0(bin2display_6_a), .in1({7{1'b0}}), .out(x7_5), .sel(demultiplexer_1_out3));
  Multiplexer #(.width(7), .enable("false")) multiplexer_5 (
    .in0(bin2display_7_a), .in1({7{1'b0}}), .out(x7_6), .sel(demultiplexer_1_out4));
  Demultiplexer #(.select(3), .enable("false")) demultiplexer_1 (
    .out0(demultiplexer_1_out0), .out1(demultiplexer_1_out1), .out2(demultiplexer_1_out2),
    .out3(demultiplexer_1_out3), .out4(demultiplexer_1_out4), .in(counter_1_q[6]), .sel(clock24h_1_set_status));  // open: out5, out6, out7
  Multiplexer #(.width(7), .enable("false")) multiplexer_6 (
    .in0(bin2display_8_a), .in1({7{1'b0}}), .out(x7_7), .sel(demultiplexer_1_out4));
  binary_to_display_code bin2display_1 (
    .b0(clock24h_1_b00), .b1(clock24h_1_b01), .b2(clock24h_1_b02), .b3(clock24h_1_b03), .a(x7_0[0]),
    .b(x7_0[1]), .c(x7_0[2]), .d(x7_0[3]), .e(x7_0[4]), .f(x7_0[5]), .g(x7_0[6]));

  // Notes on the sheet:
  //   set_on
endmodule

module counter_0to5 (
  input  a2,
  input  a1,
  input  a0,
  input  n,
  input  countdown,
  output b2,
  output b1,
  output b0,
  output n_out
);

  wire and_1_out, and_2_out, and_3_out, and_4_out, and_5_out, and_6_out, and_7_out, and_8_out, and_9_out,
       and_10_out, and_11_out, and_12_out, and_13_out, and_14_out, and_15_out, and_16_out, not_1_out,
       not_2_out, not_3_out, not_4_out, not_5_out, not_6_out, not_7_out, not_8_out, not_9_out, not_10_out,
       not_11_out, not_12_out, not_13_out, not_14_out, not_15_out, not_16_out, not_17_out, not_18_out,
       not_19_out, not_20_out, not_21_out, not_22_out, not_23_out, not_24_out, not_25_out, not_26_out,
       not_27_out, not_28_out, not_29_out, not_30_out, not_31_out, not_32_out, not_33_out, not_34_out,
       not_35_out;

  not not_1 (not_1_out, countdown);
  not not_2 (not_2_out, a2);
  not not_3 (not_3_out, countdown);
  not not_4 (not_4_out, a1);
  not not_5 (not_5_out, a0);
  not not_6 (not_6_out, a1);
  not not_7 (not_7_out, n);
  not not_8 (not_8_out, a2);
  not not_9 (not_9_out, a1);
  not not_10 (not_10_out, a0);
  not not_11 (not_11_out, a1);
  not not_12 (not_12_out, countdown);
  not not_13 (not_13_out, a2);
  not not_14 (not_14_out, a1);
  not not_15 (not_15_out, countdown);
  not not_16 (not_16_out, a2);
  not not_17 (not_17_out, a0);
  not not_18 (not_18_out, a2);
  not not_19 (not_19_out, n);
  not not_20 (not_20_out, a2);
  not not_21 (not_21_out, a1);
  not not_22 (not_22_out, a0);
  not not_23 (not_23_out, a2);
  not not_24 (not_24_out, a0);
  not not_25 (not_25_out, a1);
  not not_26 (not_26_out, a0);
  not not_27 (not_27_out, a2);
  not not_28 (not_28_out, n);
  not not_29 (not_29_out, a1);
  not not_30 (not_30_out, n);
  not not_31 (not_31_out, countdown);
  not not_32 (not_32_out, a1);
  not not_33 (not_33_out, a2);
  not not_34 (not_34_out, a1);
  not not_35 (not_35_out, a0);
  and and_1 (and_1_out, not_1_out, not_2_out, a1, a0, n);
  and and_2 (and_2_out, not_3_out, a2, not_4_out, not_5_out);
  and and_3 (and_3_out, a2, not_6_out, not_7_out);
  and and_4 (and_4_out, countdown, not_8_out, not_9_out, not_10_out, n);
  and and_5 (and_5_out, countdown, a2, not_11_out, a0);
  and and_6 (and_6_out, not_12_out, not_13_out, not_14_out, a0, n);
  and and_7 (and_7_out, not_15_out, not_16_out, a1, not_17_out);
  and and_8 (and_8_out, not_18_out, a1, not_19_out);
  and and_9 (and_9_out, countdown, not_20_out, a1, a0);
  and and_10 (and_10_out, countdown, a2, not_21_out, not_22_out, n);
  and and_11 (and_11_out, not_23_out, not_24_out, n);
  and and_12 (and_12_out, not_25_out, not_26_out, n);
  and and_13 (and_13_out, not_27_out, a0, not_28_out);
  and and_14 (and_14_out, not_29_out, a0, not_30_out);
  and and_15 (and_15_out, not_31_out, a2, not_32_out, a0, n);
  and and_16 (and_16_out, countdown, not_33_out, not_34_out, not_35_out, n);
  or or_1 (b2, and_1_out, and_2_out, and_3_out, and_4_out, and_5_out);
  or or_2 (b1, and_6_out, and_7_out, and_8_out, and_9_out, and_10_out);
  or or_3 (b0, and_11_out, and_12_out, and_13_out, and_14_out);
  or or_4 (n_out, and_15_out, and_16_out);
endmodule

module counter_0to9 (
  input  a3,
  input  a2,
  input  a1,
  input  a0,
  input  n,
  input  countdown,
  output b3,
  output b2,
  output b1,
  output b0,
  output n_out
);

  wire and_1_out, and_2_out, and_3_out, and_4_out, and_5_out, and_6_out, and_7_out, and_8_out, and_9_out,
       and_10_out, and_11_out, and_12_out, and_13_out, and_14_out, and_15_out, and_16_out, and_17_out,
       and_18_out, and_19_out, and_20_out, and_21_out, and_22_out, and_23_out, not_1_out, not_2_out,
       not_3_out, not_4_out, not_5_out, not_6_out, not_7_out, not_8_out, not_9_out, not_10_out, not_11_out,
       not_12_out, not_13_out, not_14_out, not_15_out, not_16_out, not_17_out, not_18_out, not_19_out,
       not_20_out, not_21_out, not_22_out, not_23_out, not_24_out, not_25_out, not_26_out, not_27_out,
       not_28_out, not_29_out, not_30_out, not_31_out, not_32_out, not_33_out, not_34_out, not_35_out,
       not_36_out, not_37_out, not_38_out, not_39_out, not_40_out, not_41_out, not_42_out, not_43_out,
       not_44_out, not_45_out, not_46_out, not_47_out, not_48_out, not_49_out, not_50_out, not_51_out,
       not_52_out, not_53_out, not_54_out, not_55_out, not_56_out, not_57_out, not_58_out, not_59_out,
       not_60_out, not_61_out;

  not not_1 (not_1_out, countdown);
  not not_2 (not_2_out, a3);
  not not_3 (not_3_out, a3);
  not not_4 (not_4_out, a2);
  not not_5 (not_5_out, a1);
  not not_6 (not_6_out, a0);
  not not_7 (not_7_out, countdown);
  not not_8 (not_8_out, a3);
  not not_9 (not_9_out, a2);
  not not_10 (not_10_out, a2);
  not not_11 (not_11_out, a1);
  not not_12 (not_12_out, a0);
  not not_13 (not_13_out, a3);
  not not_14 (not_14_out, a1);
  not not_15 (not_15_out, a0);
  not not_16 (not_16_out, a2);
  not not_17 (not_17_out, a1);
  not not_18 (not_18_out, a0);
  not not_19 (not_19_out, a2);
  not not_20 (not_20_out, a1);
  not not_21 (not_21_out, a0);
  not not_22 (not_22_out, a2);
  not not_23 (not_23_out, a1);
  not not_24 (not_24_out, n);
  not not_25 (not_25_out, countdown);
  not not_26 (not_26_out, a2);
  not not_27 (not_27_out, a1);
  not not_28 (not_28_out, a3);
  not not_29 (not_29_out, a2);
  not not_30 (not_30_out, a1);
  not not_31 (not_31_out, a0);
  not not_32 (not_32_out, countdown);
  not not_33 (not_33_out, a2);
  not not_34 (not_34_out, a1);
  not not_35 (not_35_out, a0);
  not not_36 (not_36_out, a2);
  not not_37 (not_37_out, a1);
  not not_38 (not_38_out, n);
  not not_39 (not_39_out, a2);
  not not_40 (not_40_out, a1);
  not not_41 (not_41_out, countdown);
  not not_42 (not_42_out, a3);
  not not_43 (not_43_out, a1);
  not not_44 (not_44_out, a3);
  not not_45 (not_45_out, n);
  not not_46 (not_46_out, a3);
  not not_47 (not_47_out, a0);
  not not_48 (not_48_out, a3);
  not not_49 (not_49_out, countdown);
  not not_50 (not_50_out, a3);
  not not_51 (not_51_out, a1);
  not not_52 (not_52_out, countdown);
  not not_53 (not_53_out, a3);
  not not_54 (not_54_out, a0);
  not not_55 (not_55_out, a3);
  not not_56 (not_56_out, n);
  not not_57 (not_57_out, a3);
  not not_58 (not_58_out, a3);
  not not_59 (not_59_out, a0);
  and and_1 (and_1_out, not_58_out, not_59_out, n);
  and and_2 (and_2_out, not_19_out, not_20_out, not_21_out, n);
  not not_60 (not_60_out, a3);
  and and_3 (and_3_out, not_60_out, a0, not_61_out);
  not not_61 (not_61_out, n);
  and and_4 (and_4_out, not_22_out, not_23_out, a0, not_24_out);
  and and_5 (and_5_out, not_1_out, not_2_out, a2, a1, a0, n);
  and and_6 (and_6_out, not_32_out, a3, not_33_out, not_34_out, not_35_out);
  and and_7 (and_7_out, a3, not_36_out, not_37_out, not_38_out);
  and and_8 (and_8_out, countdown, not_3_out, not_4_out, not_5_out, not_6_out, n);
  and and_9 (and_9_out, countdown, a3, not_39_out, not_40_out, a0);
  and and_10 (and_10_out, not_7_out, not_8_out, not_9_out, a1, a0, n);
  and and_11 (and_11_out, not_41_out, not_42_out, a2, not_43_out);
  and and_12 (and_12_out, not_44_out, a2, not_45_out);
  and and_13 (and_13_out, not_46_out, a2, a1, not_47_out);
  and and_14 (and_14_out, countdown, not_48_out, a2, a0);
  and and_15 (and_15_out, countdown, a3, not_10_out, not_11_out, not_12_out, n);
  and and_16 (and_16_out, not_49_out, not_50_out, not_51_out, a0, n);
  and and_17 (and_17_out, not_52_out, not_53_out, a1, not_54_out);
  and and_18 (and_18_out, not_55_out, a1, not_56_out);
  and and_19 (and_19_out, countdown, not_57_out, a1, a0);
  and and_20 (and_20_out, countdown, not_13_out, a2, not_14_out, not_15_out, n);
  and and_21 (and_21_out, countdown, a3, not_16_out, not_17_out, not_18_out, n);
  or or_1 (b0, and_1_out, and_2_out, and_3_out, and_4_out);
  and and_22 (and_22_out, not_25_out, a3, not_26_out, not_27_out, a0, n);
  or or_2 (n_out, and_22_out, and_23_out);
  and and_23 (and_23_out, countdown, not_28_out, not_29_out, not_30_out, not_31_out, n);
  or or_3 (b3, and_5_out, and_6_out, and_7_out, and_8_out, and_9_out);
  or or_4 (b2, and_10_out, and_11_out, and_12_out, and_13_out, and_14_out, and_15_out);
  or or_5 (b1, and_16_out, and_17_out, and_18_out, and_19_out, and_20_out, and_21_out);
endmodule

module counter24 (
  input  z1_in,
  input  z0_in,
  input  b3,
  input  b2,
  input  b1,
  input  b0,
  input  countdown,
  input  n,
  output z1,
  output z0,
  output e3,
  output e2,
  output e1,
  output e0
);

  wire and_1_out, and_2_out, and_3_out, and_4_out, and_5_out, and_6_out, and_7_out, and_8_out, and_9_out,
       and_10_out, and_11_out, and_12_out, and_13_out, and_14_out, and_15_out, and_16_out, and_17_out,
       and_18_out, and_19_out, and_20_out, and_21_out, and_22_out, and_23_out, and_24_out, and_25_out,
       and_26_out, and_27_out, and_28_out, and_29_out, and_30_out, and_31_out, and_32_out, and_33_out,
       and_34_out, and_35_out, and_36_out, and_37_out, and_38_out, and_39_out, and_40_out, and_41_out,
       and_42_out, and_43_out, and_44_out, not_1_out, not_2_out, not_3_out, not_4_out, not_5_out, not_6_out,
       not_7_out, not_8_out, not_9_out, not_10_out, not_11_out, not_12_out, not_13_out, not_14_out,
       not_15_out, not_16_out, not_17_out, not_18_out, not_19_out, not_20_out, not_21_out, not_22_out,
       not_23_out, not_24_out, not_25_out, not_26_out, not_27_out, not_28_out, not_29_out, not_30_out,
       not_31_out, not_32_out, not_33_out, not_34_out, not_35_out, not_36_out, not_37_out, not_38_out,
       not_39_out, not_40_out, not_41_out, not_42_out, not_43_out, not_44_out, not_45_out, not_46_out,
       not_47_out, not_48_out, not_49_out, not_50_out, not_51_out, not_52_out, not_53_out, not_54_out,
       not_55_out, not_56_out, not_57_out, not_58_out, not_59_out, not_60_out, not_61_out, not_62_out,
       not_63_out, not_64_out, not_65_out, not_66_out, not_67_out, not_68_out, not_69_out, not_70_out,
       not_71_out, not_72_out, not_73_out, not_74_out, not_75_out, not_76_out, not_77_out, not_78_out,
       not_79_out, not_80_out, not_81_out, not_82_out, not_83_out, not_84_out, not_85_out, not_86_out,
       not_87_out, not_88_out, not_89_out, not_90_out, not_91_out, not_92_out, not_93_out, not_94_out,
       not_95_out, not_96_out, not_97_out, not_98_out, not_99_out, not_100_out, not_101_out, not_102_out,
       not_103_out, not_104_out, not_105_out, not_106_out, not_107_out, not_108_out, not_109_out,
       not_110_out, not_111_out, not_112_out, not_113_out, not_114_out, not_115_out, not_116_out,
       not_117_out, not_118_out, not_119_out, not_120_out, not_121_out, not_122_out, not_123_out,
       not_124_out, not_125_out, not_126_out, not_127_out, not_128_out, not_129_out, not_130_out,
       not_131_out, not_132_out, not_133_out, not_134_out, not_135_out, not_136_out, not_137_out,
       not_138_out, not_139_out, not_140_out, not_141_out, not_142_out, not_143_out, not_144_out,
       not_145_out, not_146_out, not_147_out, not_148_out, not_149_out, not_150_out, not_151_out,
       not_152_out, not_153_out, not_154_out, not_155_out, not_156_out, not_157_out, not_158_out,
       not_159_out, not_160_out, not_161_out, not_162_out, not_163_out;

  not not_1 (not_1_out, countdown);
  not not_2 (not_2_out, z1_in);
  not not_3 (not_3_out, b2);
  not not_4 (not_4_out, b1);
  not not_5 (not_5_out, countdown);
  not not_6 (not_6_out, z0_in);
  not not_7 (not_7_out, b3);
  not not_8 (not_8_out, b2);
  not not_9 (not_9_out, b1);
  not not_10 (not_10_out, z0_in);
  not not_11 (not_11_out, b3);
  not not_12 (not_12_out, b2);
  not not_13 (not_13_out, n);
  not not_14 (not_14_out, z0_in);
  not not_15 (not_15_out, b3);
  not not_16 (not_16_out, b2);
  not not_17 (not_17_out, b0);
  not not_18 (not_18_out, z0_in);
  not not_19 (not_19_out, b3);
  not not_20 (not_20_out, b2);
  not not_21 (not_21_out, countdown);
  not not_22 (not_22_out, z1_in);
  not not_23 (not_23_out, z0_in);
  not not_24 (not_24_out, b2);
  not not_25 (not_25_out, b1);
  not not_26 (not_26_out, countdown);
  not not_27 (not_27_out, z1_in);
  not not_28 (not_28_out, b3);
  not not_29 (not_29_out, z1_in);
  not not_30 (not_30_out, b2);
  not not_31 (not_31_out, b1);
  not not_32 (not_32_out, n);
  not not_33 (not_33_out, z1_in);
  not not_34 (not_34_out, b3);
  not not_35 (not_35_out, z1_in);
  not not_36 (not_36_out, b3);
  not not_37 (not_37_out, z1_in);
  not not_38 (not_38_out, b2);
  not not_39 (not_39_out, b1);
  not not_40 (not_40_out, b0);
  not not_41 (not_41_out, z1_in);
  not not_42 (not_42_out, b2);
  not not_43 (not_43_out, b1);
  not not_44 (not_44_out, z0_in);
  not not_45 (not_45_out, b3);
  not not_46 (not_46_out, b2);
  not not_47 (not_47_out, b1);
  not not_48 (not_48_out, b0);
  not not_49 (not_49_out, countdown);
  not not_50 (not_50_out, z1_in);
  not not_51 (not_51_out, b3);
  not not_52 (not_52_out, countdown);
  not not_53 (not_53_out, z1_in);
  not not_54 (not_54_out, b2);
  not not_55 (not_55_out, b1);
  not not_56 (not_56_out, b0);
  not not_57 (not_57_out, z1_in);
  not not_58 (not_58_out, b2);
  not not_59 (not_59_out, b1);
  not not_60 (not_60_out, n);
  not not_61 (not_61_out, z1_in);
  not not_62 (not_62_out, b2);
  not not_63 (not_63_out, b1);
  not not_64 (not_64_out, z1_in);
  not not_65 (not_65_out, b3);
  not not_66 (not_66_out, b2);
  not not_67 (not_67_out, b1);
  not not_68 (not_68_out, b0);
  not not_69 (not_69_out, z0_in);
  not not_70 (not_70_out, b3);
  not not_71 (not_71_out, b2);
  not not_72 (not_72_out, b1);
  not not_73 (not_73_out, b0);
  not not_74 (not_74_out, countdown);
  not not_75 (not_75_out, z1_in);
  not not_76 (not_76_out, b3);
  not not_77 (not_77_out, b2);
  not not_78 (not_78_out, countdown);
  not not_79 (not_79_out, z1_in);
  not not_80 (not_80_out, b3);
  not not_81 (not_81_out, b1);
  not not_82 (not_82_out, z1_in);
  not not_83 (not_83_out, b3);
  not not_84 (not_84_out, n);
  not not_85 (not_85_out, z1_in);
  not not_86 (not_86_out, b3);
  not not_87 (not_87_out, b0);
  not not_88 (not_88_out, z1_in);
  not not_89 (not_89_out, b3);
  not not_90 (not_90_out, z1_in);
  not not_91 (not_91_out, b2);
  not not_92 (not_92_out, b1);
  not not_93 (not_93_out, b0);
  not not_94 (not_94_out, z1_in);
  not not_95 (not_95_out, b3);
  not not_96 (not_96_out, b1);
  not not_97 (not_97_out, countdown);
  not not_98 (not_98_out, z0_in);
  not not_99 (not_99_out, b3);
  not not_100 (not_100_out, b2);
  not not_101 (not_101_out, b1);
  not not_102 (not_102_out, countdown);
  not not_103 (not_103_out, z1_in);
  not not_104 (not_104_out, b3);
  not not_105 (not_105_out, b0);
  not not_106 (not_106_out, countdown);
  not not_107 (not_107_out, z1_in);
  not not_108 (not_108_out, b3);
  not not_109 (not_109_out, n);
  not not_110 (not_110_out, z0_in);
  not not_111 (not_111_out, b3);
  not not_112 (not_112_out, b2);
  not not_113 (not_113_out, b0);
  not not_114 (not_114_out, countdown);
  not not_115 (not_115_out, z0_in);
  not not_116 (not_116_out, b3);
  not not_117 (not_117_out, b2);
  not not_118 (not_118_out, n);
  not not_119 (not_119_out, z1_in);
  not not_120 (not_120_out, b3);
  not not_121 (not_121_out, z0_in);
  not not_122 (not_122_out, b3);
  not not_123 (not_123_out, b2);
  not not_124 (not_124_out, z1_in);
  not not_125 (not_125_out, b3);
  not not_126 (not_126_out, b1);
  not not_127 (not_127_out, b0);
  not not_128 (not_128_out, z1_in);
  not not_129 (not_129_out, b2);
  not not_130 (not_130_out, b1);
  not not_131 (not_131_out, b0);
  not not_132 (not_132_out, z1_in);
  not not_133 (not_133_out, b3);
  not not_134 (not_134_out, b0);
  not not_135 (not_135_out, countdown);
  not not_136 (not_136_out, z1_in);
  not not_137 (not_137_out, b3);
  not not_138 (not_138_out, n);
  not not_139 (not_139_out, z1_in);
  not not_140 (not_140_out, b2);
  not not_141 (not_141_out, b1);
  not not_142 (not_142_out, n);
  not not_143 (not_143_out, z0_in);
  not not_144 (not_144_out, b3);
  not not_145 (not_145_out, b2);
  not not_146 (not_146_out, n);
  not not_147 (not_147_out, z1_in);
  not not_148 (not_148_out, b3);
  not not_149 (not_149_out, b0);
  not not_150 (not_150_out, z1_in);
  not not_151 (not_151_out, b3);
  not not_152 (not_152_out, b0);
  not not_153 (not_153_out, z1_in);
  not not_154 (not_154_out, b2);
  not not_155 (not_155_out, b1);
  not not_156 (not_156_out, b0);
  not not_157 (not_157_out, z1_in);
  not not_158 (not_158_out, b3);
  not not_159 (not_159_out, b0);
  not not_160 (not_160_out, z0_in);
  not not_161 (not_161_out, b3);
  not not_162 (not_162_out, b2);
  not not_163 (not_163_out, b0);
  and and_1 (and_1_out, not_1_out, not_2_out, z0_in, b3, not_3_out, not_4_out, b0, n);
  and and_2 (and_2_out, not_5_out, z1_in, not_6_out, not_7_out, not_8_out, not_9_out);
  and and_3 (and_3_out, z1_in, not_10_out, not_11_out, not_12_out, not_13_out);
  and and_4 (and_4_out, z1_in, not_14_out, not_15_out, not_16_out, b1, not_17_out);
  and and_5 (and_5_out, countdown, z1_in, not_18_out, not_19_out, not_20_out, b0);
  and and_6 (and_6_out, not_21_out, not_22_out, not_23_out, b3, not_24_out, not_25_out, b0, n);
  and and_7 (and_7_out, not_26_out, not_27_out, z0_in, not_28_out);
  and and_8 (and_8_out, not_29_out, z0_in, not_30_out, not_31_out, not_32_out);
  and and_9 (and_9_out, not_33_out, z0_in, not_34_out, b1);
  and and_10 (and_10_out, not_35_out, z0_in, not_36_out, b2);
  and and_11 (and_11_out, not_37_out, z0_in, b3, not_38_out, not_39_out, not_40_out);
  and and_12 (and_12_out, countdown, not_41_out, z0_in, not_42_out, not_43_out, b0);
  and and_13 (and_13_out, countdown, z1_in, not_44_out, not_45_out, not_46_out, not_47_out, not_48_out, n);
  and and_14 (and_14_out, not_49_out, not_50_out, not_51_out, b2, b1, b0, n);
  and and_15 (and_15_out, not_52_out, not_53_out, b3, not_54_out, not_55_out, not_56_out);
  and and_16 (and_16_out, not_57_out, b3, not_58_out, not_59_out, not_60_out);
  and and_17 (and_17_out, countdown, not_61_out, b3, not_62_out, not_63_out, b0);
  and and_18 (and_18_out, countdown, not_64_out, z0_in, not_65_out, not_66_out, not_67_out, not_68_out, n);
  and and_19 (and_19_out, countdown, z1_in, not_69_out, not_70_out, not_71_out, not_72_out, not_73_out, n);
  and and_20 (and_20_out, not_74_out, not_75_out, not_76_out, not_77_out, b1, b0, n);
  and and_21 (and_21_out, not_78_out, not_79_out, not_80_out, b2, not_81_out);
  and and_22 (and_22_out, not_82_out, not_83_out, b2, not_84_out);
  and and_23 (and_23_out, not_85_out, not_86_out, b2, b1, not_87_out);
  and and_24 (and_24_out, countdown, not_88_out, not_89_out, b2, b0);
  and and_25 (and_25_out, countdown, not_90_out, b3, not_91_out, not_92_out, not_93_out, n);
  and and_26 (and_26_out, not_94_out, not_95_out, not_96_out, b0, not_97_out, n);
  and and_27 (and_27_out, not_98_out, not_99_out, not_100_out, not_101_out, b0, not_102_out, n);
  and and_28 (and_28_out, not_103_out, not_104_out, b1, not_105_out, not_106_out);
  and and_29 (and_29_out, not_107_out, not_108_out, b1, not_109_out);
  and and_30 (and_30_out, not_110_out, not_111_out, not_112_out, b1, not_113_out, not_114_out);
  and and_31 (and_31_out, not_115_out, not_116_out, not_117_out, b1, not_118_out);
  and and_32 (and_32_out, not_119_out, not_120_out, b1, b0, countdown);
  and and_33 (and_33_out, not_121_out, not_122_out, not_123_out, b1, b0, countdown);
  and and_34 (and_34_out, not_124_out, not_125_out, b2, not_126_out, not_127_out, countdown, n);
  and and_35 (and_35_out, not_128_out, b3, not_129_out, not_130_out, not_131_out, countdown, n);
  and and_36 (and_36_out, not_132_out, not_133_out, not_134_out, not_135_out, n);
  and and_37 (and_37_out, not_136_out, not_137_out, b0, not_138_out);
  and and_38 (and_38_out, not_139_out, not_140_out, not_141_out, b0, not_142_out);
  and and_39 (and_39_out, not_143_out, not_144_out, not_145_out, b0, not_146_out);
  and and_40 (and_40_out, not_147_out, not_148_out, b1, not_149_out, n);
  and and_41 (and_41_out, not_150_out, not_151_out, b2, not_152_out, n);
  and and_42 (and_42_out, not_153_out, b3, not_154_out, not_155_out, not_156_out, n);
  and and_43 (and_43_out, not_157_out, z0_in, not_158_out, not_159_out, n);
  and and_44 (and_44_out, z1_in, not_160_out, not_161_out, not_162_out, not_163_out, n);
  or or_1 (z1, and_1_out, and_2_out, and_3_out, and_4_out, and_5_out);
  or or_2 (z0, and_6_out, and_7_out, and_8_out, and_9_out, and_10_out, and_11_out, and_12_out, and_13_out);
  or or_3 (e3, and_14_out, and_15_out, and_16_out, and_17_out, and_18_out, and_19_out);
  or or_4 (e2, and_20_out, and_21_out, and_22_out, and_23_out, and_24_out, and_25_out);
  or or_5 (e1, and_26_out, and_27_out, and_28_out, and_29_out, and_30_out, and_31_out, and_32_out, and_33_out, and_34_out, and_35_out);
  or or_6 (e0, and_36_out, and_37_out, and_38_out, and_39_out, and_40_out, and_41_out, and_42_out, and_43_out, and_44_out);
endmodule

module timezone_adder (
  input  b60,
  input  b61,
  input  b62,
  input  b63,
  input  b70,
  input  b71,
  input  [1:0] timezone,
  output b60_out,
  output b61_out,
  output b62_out,
  output b63_out,
  output b70_out,
  output b71_out
);

  wire and_1_out, substractor_5bit_1_carry_out, substractor_5bit_2_carry_out, substractor_5bit_3_carry_out,
       substractor_5bit_4_carry_out;
  wire [4:0] adder_5bit_1_p, adder_5bit_2_p, adder_5bit_3_p, demultiplexer_1_out0, demultiplexer_1_out1,
       multiplexer_1_out, multiplexer_2_out, multiplexer_3_out, multiplexer_4_out, multiplexer_5_out,
       multiplexer_6_out, multiplexer_7_out, substractor_5bit_1_p, substractor_5bit_2_p,
       substractor_5bit_3_p, substractor_5bit_4_p;
  wire [4:2] multiplexer_9_out;
  wire [4:4] multiplexer_8_out;

  and and_1 (and_1_out, timezone[0], timezone[1]);
  Demultiplexer #(.width(5), .enable("false")) demultiplexer_1 (
    .out0(demultiplexer_1_out0), .out1(demultiplexer_1_out1), .in(multiplexer_1_out), .sel(and_1_out));
  Multiplexer #(.select(2), .width(5), .enable("false")) multiplexer_1 (
    .in0({5{1'b0}}), .in1(5'b00001), .in2(5'b00111), .in3(5'b00101), .out(multiplexer_1_out), .sel(timezone));
  Multiplexer #(.select(2), .width(5), .enable("false")) multiplexer_2 (
    .in0({5{1'b0}}), .in1(5'b01010), .in2(5'b10100), .in3({5{1'b0}}), .out(multiplexer_2_out),
    .sel({b71, b70}));
  adder_5bit adder_5bit_1 (
    .Carry_in(1'b0), .A({1'b0, b63, b62, b61, b60}), .B(multiplexer_2_out), .P(adder_5bit_1_p));  // open: Carry_out
  adder_5bit adder_5bit_3 (
    .Carry_in(1'b0), .A(adder_5bit_1_p), .B(demultiplexer_1_out0), .P(adder_5bit_3_p));  // open: Carry_out
  substractor_5bit substractor_5bit_1 (
    .carry_in(1'b0), .A(adder_5bit_1_p), .B(demultiplexer_1_out1), .P(substractor_5bit_1_p),
    .carry_out(substractor_5bit_1_carry_out));
  adder_5bit adder_5bit_2 (.Carry_in(1'b0), .A(adder_5bit_1_p), .B(5'b10011), .P(adder_5bit_2_p));  // open: Carry_out
  substractor_5bit substractor_5bit_2 (
    .carry_in(1'b0), .A(adder_5bit_3_p), .B(5'b11000), .P(substractor_5bit_2_p),
    .carry_out(substractor_5bit_2_carry_out));
  Multiplexer #(.width(5), .enable("false")) multiplexer_3 (
    .in0(substractor_5bit_1_p), .in1(adder_5bit_2_p), .out(multiplexer_3_out),
    .sel(substractor_5bit_1_carry_out));
  Multiplexer #(.width(5), .enable("false")) multiplexer_4 (
    .in0(substractor_5bit_2_p), .in1(adder_5bit_3_p), .out(multiplexer_4_out),
    .sel(substractor_5bit_2_carry_out));
  Multiplexer #(.width(5), .enable("false")) multiplexer_5 (
    .in0(multiplexer_4_out), .in1(multiplexer_3_out), .out(multiplexer_5_out), .sel(and_1_out));
  substractor_5bit substractor_5bit_3 (
    .carry_in(1'b0), .A(multiplexer_5_out), .B(5'b10100), .P(substractor_5bit_3_p),
    .carry_out(substractor_5bit_3_carry_out));
  substractor_5bit substractor_5bit_4 (
    .carry_in(1'b0), .A(multiplexer_5_out), .B(5'b01010), .P(substractor_5bit_4_p),
    .carry_out(substractor_5bit_4_carry_out));
  Multiplexer #(.width(5), .enable("false")) multiplexer_6 (
    .in0(substractor_5bit_4_p), .in1(multiplexer_5_out), .out(multiplexer_6_out),
    .sel(substractor_5bit_4_carry_out));
  Multiplexer #(.width(5), .enable("false")) multiplexer_7 (
    .in0(5'b00001), .in1({5{1'b0}}), .out(multiplexer_7_out), .sel(substractor_5bit_4_carry_out));
  Multiplexer #(.width(5), .enable("false")) multiplexer_8 (
    .in0(substractor_5bit_3_p), .in1(multiplexer_6_out),
    .out({multiplexer_8_out[4], b63_out, b62_out, b61_out, b60_out}), .sel(substractor_5bit_3_carry_out));
  Multiplexer #(.width(5), .enable("false")) multiplexer_9 (
    .in0(5'b00010), .in1(multiplexer_7_out), .out({multiplexer_9_out, b71_out, b70_out}),
    .sel(substractor_5bit_3_carry_out));

  // Notes on the sheet:
  //   =10
  //   =20
  //   =0
  //   actual time (24h)
  //   calculate -5
  //   if underflow : calculate +19
  //   minus 24
  //   divide time in b6 and b7
  //   minus 20
  //   minus 10
endmodule

module state1_timezone (
  input  b1_long,
  input  dip_switch,
  input  b1_short,
  input  b2_short,
  input  clk_100th,
  input  reset,
  output [6:0] x7_7,
  output [6:0] x7_6,
  output [6:0] x7_5,
  output [6:0] x7_3,
  output [6:0] x7_2,
  output [1:0] timezone,
  output set_on
);

  wire and_1_out, and_2_out, and_3_out, d_ff_1_q, d_ff_2_q, not_1_out, switch_state_machine_1_b0,
       switch_state_machine_1_b1, timezone_changer_1_zone0, timezone_changer_1_zone1;
  wire [6:0] timezonecode_display_1_x7_2, timezonecode_display_1_x7_3, timezonecode_display_1_x7_5,
       timezonecode_display_1_x7_6, timezonecode_display_1_x7_7;
  wire [7:0] counter_1_q;

  and and_1 (and_1_out, b1_long, ~dip_switch);  // AND_Gate
  state1_switch_state_machine switch_state_machine_1 (
    .state_b1(d_ff_1_q), .state_b0(d_ff_2_q), .in_e8f0e200(and_1_out), .b1(switch_state_machine_1_b1),
    .b0(switch_state_machine_1_b0), .set_on(set_on));
  and and_2 (and_2_out, set_on, b1_short);
  and and_3 (and_3_out, set_on, b2_short);
  D_Flip_Flop d_ff_1 (
    .D(switch_state_machine_1_b1), .clk(clk_100th), .Q(d_ff_1_q), .reset(dip_switch));  // open: Qn, preset
  D_Flip_Flop d_ff_2 (
    .D(switch_state_machine_1_b0), .clk(clk_100th), .Q(d_ff_2_q), .reset(dip_switch));  // open: Qn, preset
  Counter counter_1 (
    .clr(not_1_out), .load(1'b0), .up(1'b1), .clk(clk_100th), .Q(counter_1_q));  // open: count, D, carry
  not not_1 (not_1_out, set_on);
  state1_timezone_changer timezone_changer_1 (
    .b1_short(and_2_out), .b2_short(and_3_out), .zon1_in(timezone[1]), .zone0_in(timezone[0]),
    .zone1(timezone_changer_1_zone1), .zone0(timezone_changer_1_zone0));
  D_Flip_Flop d_ff_3 (
    .D(timezone_changer_1_zone1), .clk(clk_100th), .Q(timezone[1]), .reset(reset));  // open: Qn, preset
  D_Flip_Flop d_ff_4 (
    .D(timezone_changer_1_zone0), .clk(clk_100th), .Q(timezone[0]), .reset(reset));  // open: Qn, preset
  state1_timezonecode_display timezonecode_display_1 (
    .timezone(timezone), .x7_7(timezonecode_display_1_x7_7), .x7_6(timezonecode_display_1_x7_6),
    .x7_5(timezonecode_display_1_x7_5), .x7_3(timezonecode_display_1_x7_3), .x7_2(timezonecode_display_1_x7_2));
  Multiplexer #(.width(7), .enable("false")) multiplexer_1 (
    .in0(timezonecode_display_1_x7_7), .in1({7{1'b0}}), .out(x7_7), .sel(counter_1_q[6]));
  Multiplexer #(.width(7), .enable("false")) multiplexer_2 (
    .in0(timezonecode_display_1_x7_6), .in1({7{1'b0}}), .out(x7_6), .sel(counter_1_q[6]));
  Multiplexer #(.width(7), .enable("false")) multiplexer_3 (
    .in0(timezonecode_display_1_x7_5), .in1({7{1'b0}}), .out(x7_5), .sel(counter_1_q[6]));
  Multiplexer #(.width(7), .enable("false")) multiplexer_4 (
    .in0(timezonecode_display_1_x7_3), .in1({7{1'b0}}), .out(x7_3), .sel(counter_1_q[6]));
  Multiplexer #(.width(7), .enable("false")) multiplexer_5 (
    .in0(timezonecode_display_1_x7_2), .in1({7{1'b0}}), .out(x7_2), .sel(counter_1_q[6]));

  // Notes on the sheet:
  //   set_on
  //   lets the display blink
  //   current timezone
endmodule

module state1_timezone_changer (
  input  b1_short,
  input  b2_short,
  input  zon1_in,
  input  zone0_in,
  output zone1,
  output zone0
);

  wire and_1_out, and_2_out, and_3_out, and_4_out, and_5_out, and_6_out, and_7_out, and_8_out, not_1_out,
       not_2_out, not_3_out, not_4_out, not_5_out, not_6_out, not_7_out, not_8_out, not_9_out, not_10_out,
       not_11_out, not_12_out;

  not not_1 (not_1_out, b1_short);
  not not_2 (not_2_out, b2_short);
  not not_3 (not_3_out, b1_short);
  not not_4 (not_4_out, b1_short);
  not not_5 (not_5_out, zon1_in);
  not not_6 (not_6_out, zone0_in);
  not not_7 (not_7_out, zon1_in);
  not not_8 (not_8_out, zone0_in);
  not not_9 (not_9_out, b1_short);
  not not_10 (not_10_out, b2_short);
  not not_11 (not_11_out, zone0_in);
  not not_12 (not_12_out, zone0_in);
  and and_1 (and_1_out, not_1_out, not_2_out, zon1_in);
  and and_2 (and_2_out, not_3_out, zon1_in, zone0_in);
  and and_3 (and_3_out, not_4_out, b2_short, not_5_out, not_6_out);
  and and_4 (and_4_out, b1_short, not_7_out, zone0_in);
  and and_5 (and_5_out, b1_short, zon1_in, not_8_out);
  and and_6 (and_6_out, not_9_out, not_10_out, zone0_in);
  and and_7 (and_7_out, b2_short, not_11_out);
  and and_8 (and_8_out, b1_short, not_12_out);
  or or_1 (zone1, and_1_out, and_2_out, and_3_out, and_4_out, and_5_out);
  or or_2 (zone0, and_6_out, and_7_out, and_8_out);
endmodule

module state1_timezonecode_display (
  input  [1:0] timezone,
  output [6:0] x7_7,
  output [6:0] x7_6,
  output [6:0] x7_5,
  output [6:0] x7_3,
  output [6:0] x7_2
);

  wire [3:0] multiplexer_1_out;
  wire [6:6] and_1_out;

  Multiplexer #(.select(2), .width(4), .enable("false")) multiplexer_1 (
    .in0(4'b0000), .in1(4'b0001), .in2(4'b0111), .in3(4'b0101), .out(multiplexer_1_out), .sel(timezone));
  Multiplexer #(.select(2), .width(21), .enable("false")) multiplexer_2 (
    .in0(21'h152e38), .in1(21'h143cfc), .in2(21'h153bf6), .in3(21'h11a35c), .out({x7_5, x7_6, x7_7}),
    .sel(timezone));
  and and_1 (and_1_out[6], timezone[0], timezone[1]);
  assign x7_3 = 7'b1000000 & {7{and_1_out[6]}};  // AND_Gate and_2, 7 bits wide
  binary_to_display_code binary_to_display_code_1 (
    .b0(multiplexer_1_out[0]), .b1(multiplexer_1_out[1]), .b2(multiplexer_1_out[2]),
    .b3(multiplexer_1_out[3]), .a(x7_2[0]), .b(x7_2[1]), .c(x7_2[2]), .d(x7_2[3]), .e(x7_2[4]), .f(x7_2[5]),
    .g(x7_2[6]));

  // Notes on the sheet:
  //   L
  //   O
  //   N
  //   B
  //   E
  //   R
  //   A
  //   N
  //   T
  //   T
  //   H
  //   O
  //   for Ottawa
  //   minus
endmodule

module state1_switch_state_machine (
  input  state_b1,
  input  state_b0,
  input  in_e8f0e200,
  output b1,
  output b0,
  output set_on
);

  wire and_1_out, and_2_out, and_3_out, and_4_out, and_5_out, not_1_out, not_2_out, not_3_out, not_4_out,
       not_5_out, not_6_out;

  not not_1 (not_1_out, state_b1);
  and and_1 (and_1_out, not_1_out, state_b0, not_2_out);
  not not_2 (not_2_out, in_e8f0e200);
  and and_2 (and_2_out, state_b1, not_3_out);
  not not_3 (not_3_out, state_b0);
  and and_3 (and_3_out, state_b1, in_e8f0e200);
  not not_4 (not_4_out, state_b1);
  and and_4 (and_4_out, not_4_out, state_b0);
  not not_5 (not_5_out, state_b0);
  and and_5 (and_5_out, state_b1, not_5_out, not_6_out);
  not not_6 (not_6_out, in_e8f0e200);
  or or_1 (b1, and_1_out, and_2_out, and_3_out);
  or or_2 (set_on, and_4_out, and_5_out);

  assign b0 = in_e8f0e200;
endmodule

module state2_alarmclock (
  input  alarm,
  input  b1_short,
  input  b1_long,
  input  b2_short,
  input  clk_100th,
  input  b2_long,
  input  dip_switch,
  input  reset,
  output [6:0] x7_m1,
  output [6:0] x7_m2,
  output [6:0] x7_h1,
  output [6:0] x7_h2,
  output [6:0] x7_6,
  output [6:0] x7_7,
  output alarm_on,
  output high
);

  wire and_1_out, and_2_out, and_3_out, and_4_out, and_5_out, d_ff_2_q, d_ff_3_q, d_ff_4_q, d_ff_5_q,
       not_1_out, not_2_out, or_1_out, or_2_out, or_3_out, test_new_statemachine_b0,
       test_new_statemachine_b1, test_new_statemachine_b2, test_new_statemachine_set_h,
       test_new_statemachine_set_h2, test_new_statemachine_set_m1, test_new_statemachine_set_m2;
  wire [6:0] alarmclock_setter_1_h1, alarmclock_setter_1_h2, alarmclock_setter_1_m1, alarmclock_setter_1_m2;
  wire [6:6] nand_1_out, nand_2_out, nand_3_out;
  wire [7:0] counter_1_q;

  not not_1 (not_1_out, dip_switch);
  and and_1 (and_1_out, b2_long, not_2_out, not_1_out);
  and and_2 (and_2_out, b1_short, not_1_out);
  and and_3 (and_3_out, b1_long, not_1_out);
  and and_4 (and_4_out, b2_short, not_1_out);
  and and_5 (and_5_out, and_2_out, not_2_out);
  D_Flip_Flop d_ff_1 (.D(alarm_on), .clk(clk_100th), .Q(alarm_on), .preset(and_5_out), .reset(or_1_out));  // open: Qn
  or or_1 (or_1_out, and_1_out, reset);
  D_Flip_Flop d_ff_2 (.D(d_ff_2_q), .clk(clk_100th), .Q(d_ff_2_q), .preset(alarm), .reset(or_2_out));  // open: Qn
  or or_2 (or_2_out, and_1_out, reset);
  state2_alarmclock_statemachine test_new_statemachine (
    .b2_long(and_1_out), .alarm(d_ff_2_q), .state_b2(d_ff_3_q), .stateb_b1(d_ff_4_q), .state_b0(d_ff_5_q),
    .b1_long(and_3_out), .b2_short(and_4_out), .b2(test_new_statemachine_b2), .b1(test_new_statemachine_b1),
    .b0(test_new_statemachine_b0), .set_m1(test_new_statemachine_set_m1),
    .set_m2(test_new_statemachine_set_m2), .set_h(test_new_statemachine_set_h),
    .set_h2(test_new_statemachine_set_h2));
  alarm_melody alarm_melody_1 (.alarm_on(d_ff_2_q), .high(high));
  D_Flip_Flop d_ff_3 (.D(test_new_statemachine_b2), .clk(clk_100th), .Q(d_ff_3_q), .reset(reset));  // open: Qn, preset
  D_Flip_Flop d_ff_4 (.D(test_new_statemachine_b1), .clk(clk_100th), .Q(d_ff_4_q), .reset(reset));  // open: Qn, preset
  D_Flip_Flop d_ff_5 (.D(test_new_statemachine_b0), .clk(clk_100th), .Q(d_ff_5_q), .reset(reset));  // open: Qn, preset
  or or_3 (or_3_out, test_new_statemachine_set_m1, test_new_statemachine_set_m2, test_new_statemachine_set_h2, test_new_statemachine_set_h);
  not not_2 (not_2_out, or_3_out);
  Multiplexer #(.width(7), .enable("false")) multiplexer_1 (
    .in0(7'b1000000), .in1(7'b0111111), .out(x7_7), .sel(alarm_on));
  Multiplexer #(.width(7), .enable("false")) multiplexer_2 (
    .in0(7'b1000000), .in1(7'b1010100), .out(x7_6), .sel(alarm_on));
  Counter counter_1 (.clr(reset), .clk(clk_100th), .Q(counter_1_q));  // open: load, up, count, D, carry
  alarmclock_setter alarmclock_setter_1 (
    .increment(and_2_out), .set_h(test_new_statemachine_set_h), .set_min10(test_new_statemachine_set_m2),
    .set_min1(test_new_statemachine_set_m1), .reset(reset), .clk(clk_100th), .h1(alarmclock_setter_1_h1),
    .h2(alarmclock_setter_1_h2), .m2(alarmclock_setter_1_m2), .m1(alarmclock_setter_1_m1));
  assign x7_m1 = {7{nand_3_out[6]}} & alarmclock_setter_1_m1;  // AND_Gate and_6, 7 bits wide
  nand nand_1 (nand_1_out[6], test_new_statemachine_set_h, counter_1_q[6]);
  assign x7_m2 = {7{nand_2_out[6]}} & alarmclock_setter_1_m2;  // AND_Gate and_7, 7 bits wide
  assign x7_h1 = {7{nand_1_out[6]}} & alarmclock_setter_1_h1;  // AND_Gate and_8, 7 bits wide
  assign x7_h2 = {7{nand_1_out[6]}} & alarmclock_setter_1_h2;  // AND_Gate and_9, 7 bits wide
  nand nand_2 (nand_2_out[6], counter_1_q[6], test_new_statemachine_set_m2);
  nand nand_3 (nand_3_out[6], counter_1_q[6], test_new_statemachine_set_m1);

  // Notes on the sheet:
  //   1 = Alarm is active
  //   play music if this signal is 1
  //   O
  //   -
  //   1 = Alarm set mode
  //   n
  //   -
endmodule

module state2_alarmclock_statemachine (
  input  b2_long,
  input  alarm,
  input  state_b2,
  input  stateb_b1,
  input  state_b0,
  input  b1_long,
  input  b2_short,
  output b2,
  output b1,
  output b0,
  output set_m1,
  output set_m2,
  output set_h,
  output set_h2
);

  wire and_1_out, and_2_out, and_3_out, and_4_out, and_5_out, and_6_out, and_7_out, and_8_out, and_9_out,
       not_1_out, not_2_out, not_3_out, not_4_out, not_5_out, not_6_out, not_7_out, not_8_out, not_9_out,
       not_10_out, not_11_out, not_12_out, not_13_out, not_14_out, not_15_out, not_16_out, not_17_out,
       not_18_out, not_19_out, not_20_out, not_21_out, not_22_out, not_23_out, not_24_out, not_25_out,
       not_26_out, not_27_out, not_28_out, not_29_out, not_30_out, not_31_out, not_32_out, not_33_out,
       not_34_out, not_35_out, not_36_out, not_37_out, not_38_out, not_39_out, not_40_out, not_41_out,
       not_42_out, not_43_out, not_44_out, not_45_out;

  not not_1 (not_1_out, b2_long);
  not not_2 (not_2_out, state_b2);
  not not_3 (not_3_out, b2_long);
  not not_4 (not_4_out, b1_long);
  not not_5 (not_5_out, b2_long);
  not not_6 (not_6_out, b2_long);
  not not_7 (not_7_out, alarm);
  not not_8 (not_8_out, state_b2);
  not not_9 (not_9_out, stateb_b1);
  not not_10 (not_10_out, b2_long);
  not not_11 (not_11_out, alarm);
  not not_12 (not_12_out, state_b2);
  not not_13 (not_13_out, state_b0);
  not not_14 (not_14_out, b2_long);
  not not_15 (not_15_out, alarm);
  not not_16 (not_16_out, state_b2);
  not not_17 (not_17_out, b2_short);
  not not_18 (not_18_out, b2_long);
  not not_19 (not_19_out, alarm);
  not not_20 (not_20_out, state_b2);
  not not_21 (not_21_out, stateb_b1);
  not not_22 (not_22_out, state_b0);
  not not_23 (not_23_out, b2_long);
  not not_24 (not_24_out, alarm);
  not not_25 (not_25_out, state_b2);
  not not_26 (not_26_out, b2_short);
  not not_27 (not_27_out, b2_long);
  not not_28 (not_28_out, alarm);
  not not_29 (not_29_out, state_b2);
  not not_30 (not_30_out, state_b0);
  not not_31 (not_31_out, b2_long);
  not not_32 (not_32_out, alarm);
  not not_33 (not_33_out, state_b2);
  not not_34 (not_34_out, stateb_b1);
  not not_35 (not_35_out, b2_long);
  not not_36 (not_36_out, alarm);
  not not_37 (not_37_out, state_b2);
  not not_38 (not_38_out, state_b0);
  not not_39 (not_39_out, b2_long);
  not not_40 (not_40_out, alarm);
  not not_41 (not_41_out, state_b2);
  not not_42 (not_42_out, b2_long);
  not not_43 (not_43_out, alarm);
  not not_44 (not_44_out, stateb_b1);
  not not_45 (not_45_out, state_b0);
  and and_1 (and_1_out, not_1_out, not_2_out, stateb_b1, state_b0, b2_short);
  and and_2 (and_2_out, not_3_out, state_b2, stateb_b1, not_4_out);
  and and_3 (and_3_out, not_5_out, alarm);
  and and_4 (and_4_out, not_6_out, not_7_out, not_8_out, not_9_out, state_b0, b2_short);
  and and_5 (and_5_out, not_10_out, not_11_out, not_12_out, stateb_b1, not_13_out);
  and and_6 (and_6_out, not_14_out, not_15_out, not_16_out, stateb_b1, not_17_out);
  and and_7 (and_7_out, not_18_out, not_19_out, not_20_out, not_21_out, not_22_out, b1_long);
  and and_8 (and_8_out, not_23_out, not_24_out, not_25_out, state_b0, not_26_out);
  and and_9 (and_9_out, not_27_out, not_28_out, not_29_out, stateb_b1, not_30_out, b2_short);
  and and_10 (set_m1, not_31_out, not_32_out, not_33_out, not_34_out, state_b0);
  and and_11 (set_m2, not_35_out, not_36_out, not_37_out, stateb_b1, not_38_out);
  and and_12 (set_h, not_39_out, not_40_out, not_41_out, stateb_b1, state_b0);
  and and_13 (set_h2, not_42_out, not_43_out, state_b2, not_44_out, not_45_out);
  or or_1 (b2, and_1_out, and_2_out, and_3_out);
  or or_2 (b1, and_4_out, and_5_out, and_6_out);
  or or_3 (b0, and_7_out, and_8_out, and_9_out);
endmodule

module alarmclock_setter (
  input  increment,
  input  set_h,
  input  set_min10,
  input  set_min1,
  input  reset,
  input  clk,
  output [6:0] h1,
  output [6:0] h2,
  output [6:0] m2,
  output [6:0] m1
);

  wire and_1_out, and_2_out, and_3_out, counter24_1_e0, counter24_1_e1, counter24_1_e2, counter24_1_e3,
       counter24_1_z0, counter24_1_z1, counter_0to5_1_b0, counter_0to5_1_b1, counter_0to5_1_b2,
       counter_0to9_1_b0, counter_0to9_1_b1, counter_0to9_1_b2, counter_0to9_1_b3, d_ff_1_q, d_ff_2_q,
       d_ff_3_q, d_ff_4_q, d_ff_5_q, d_ff_6_q, d_ff_7_q, d_ff_8_q, d_ff_9_q, d_ff_10_q, d_ff_11_q, d_ff_12_q,
       d_ff_13_q;

  and and_1 (and_1_out, increment, set_h);
  and and_2 (and_2_out, set_min10, increment);
  and and_3 (and_3_out, increment, set_min1);
  counter24 counter24_1 (
    .z1_in(d_ff_1_q), .z0_in(d_ff_2_q), .b3(d_ff_3_q), .b2(d_ff_4_q), .b1(d_ff_5_q), .b0(d_ff_6_q),
    .countdown(1'b0), .n(and_1_out), .z1(counter24_1_z1), .z0(counter24_1_z0), .e3(counter24_1_e3),
    .e2(counter24_1_e2), .e1(counter24_1_e1), .e0(counter24_1_e0));
  counter_0to9 counter_0to9_1 (
    .a3(d_ff_7_q), .a2(d_ff_8_q), .a1(d_ff_9_q), .a0(d_ff_10_q), .n(and_3_out), .countdown(1'b0),
    .b3(counter_0to9_1_b3), .b2(counter_0to9_1_b2), .b1(counter_0to9_1_b1), .b0(counter_0to9_1_b0));  // open: n_out
  D_Flip_Flop d_ff_1 (.D(counter24_1_z1), .clk(clk), .Q(d_ff_1_q), .reset(reset));  // open: Qn, preset
  D_Flip_Flop d_ff_2 (.D(counter24_1_z0), .clk(clk), .Q(d_ff_2_q), .reset(reset));  // open: Qn, preset
  D_Flip_Flop d_ff_3 (.D(counter24_1_e3), .clk(clk), .Q(d_ff_3_q), .reset(reset));  // open: Qn, preset
  D_Flip_Flop d_ff_4 (.D(counter24_1_e2), .clk(clk), .Q(d_ff_4_q), .reset(reset));  // open: Qn, preset
  D_Flip_Flop d_ff_5 (.D(counter24_1_e1), .clk(clk), .Q(d_ff_5_q), .reset(reset));  // open: Qn, preset
  D_Flip_Flop d_ff_6 (.D(counter24_1_e0), .clk(clk), .Q(d_ff_6_q), .reset(reset));  // open: Qn, preset
  counter_0to5 counter_0to5_1 (
    .a2(d_ff_11_q), .a1(d_ff_12_q), .a0(d_ff_13_q), .n(and_2_out), .countdown(1'b0), .b2(counter_0to5_1_b2),
    .b1(counter_0to5_1_b1), .b0(counter_0to5_1_b0));  // open: n_out
  D_Flip_Flop d_ff_7 (.D(counter_0to9_1_b3), .clk(clk), .Q(d_ff_7_q), .reset(reset));  // open: Qn, preset
  D_Flip_Flop d_ff_8 (.D(counter_0to9_1_b2), .clk(clk), .Q(d_ff_8_q), .reset(reset));  // open: Qn, preset
  D_Flip_Flop d_ff_9 (.D(counter_0to9_1_b1), .clk(clk), .Q(d_ff_9_q), .reset(reset));  // open: Qn, preset
  D_Flip_Flop d_ff_10 (.D(counter_0to9_1_b0), .clk(clk), .Q(d_ff_10_q), .reset(reset));  // open: Qn, preset
  D_Flip_Flop d_ff_11 (.D(counter_0to5_1_b2), .clk(clk), .Q(d_ff_11_q), .reset(reset));  // open: Qn, preset
  D_Flip_Flop d_ff_12 (.D(counter_0to5_1_b1), .clk(clk), .Q(d_ff_12_q), .reset(reset));  // open: Qn, preset
  D_Flip_Flop d_ff_13 (.D(counter_0to5_1_b0), .clk(clk), .Q(d_ff_13_q), .reset(reset));  // open: Qn, preset
  binary_to_display_code counter_min10 (
    .b0(d_ff_13_q), .b1(d_ff_12_q), .b2(d_ff_11_q), .b3(1'b0), .a(m2[0]), .b(m2[1]), .c(m2[2]), .d(m2[3]),
    .e(m2[4]), .f(m2[5]), .g(m2[6]));
  binary_to_display_code counter_min1 (
    .b0(d_ff_10_q), .b1(d_ff_9_q), .b2(d_ff_8_q), .b3(d_ff_7_q), .a(m1[0]), .b(m1[1]), .c(m1[2]), .d(m1[3]),
    .e(m1[4]), .f(m1[5]), .g(m1[6]));
  binary_to_display_code binary_to_display_code_1 (
    .b0(d_ff_6_q), .b1(d_ff_5_q), .b2(d_ff_4_q), .b3(d_ff_3_q), .a(h1[0]), .b(h1[1]), .c(h1[2]), .d(h1[3]),
    .e(h1[4]), .f(h1[5]), .g(h1[6]));
  binary_to_display_code binary_to_display_code_2 (
    .b0(d_ff_2_q), .b1(d_ff_1_q), .b2(1'b0), .b3(1'b0), .a(h2[0]), .b(h2[1]), .c(h2[2]), .d(h2[3]),
    .e(h2[4]), .f(h2[5]), .g(h2[6]));
endmodule

module clock_setter_state_machine (
  input  s2,
  input  s1,
  input  s0,
  input  b1_long,
  input  b2_short,
  output s2_2b948b35,
  output s1_2101c0e9,
  output s0_21d125c7,
  output set_ten_hour,
  output set_hour,
  output set_ten_min,
  output set_min,
  output set_ten_sec,
  output set_sec
);

  wire and_1_out, and_2_out, and_3_out, and_4_out, and_5_out, and_6_out, and_7_out, and_8_out, and_9_out,
       and_10_out, and_11_out, and_12_out, and_13_out, not_1_out, not_2_out, not_3_out, not_4_out, not_5_out,
       not_6_out, not_7_out, not_8_out, not_9_out, not_10_out, not_11_out, not_12_out, not_13_out,
       not_14_out, not_15_out, not_16_out, not_17_out, not_18_out, not_19_out, not_20_out, not_21_out,
       not_22_out, not_23_out, not_24_out, not_25_out, not_26_out, not_27_out, not_28_out, not_29_out,
       not_30_out, not_31_out, not_32_out, not_33_out;

  not not_1 (not_1_out, s2);
  not not_2 (not_2_out, s1);
  not not_3 (not_3_out, b1_long);
  not not_4 (not_4_out, s0);
  not not_5 (not_5_out, b2_short);
  not not_6 (not_6_out, s1);
  not not_7 (not_7_out, s1);
  not not_8 (not_8_out, s2);
  not not_9 (not_9_out, s0);
  not not_10 (not_10_out, s2);
  not not_11 (not_11_out, b2_short);
  not not_12 (not_12_out, s0);
  not not_13 (not_13_out, b2_short);
  not not_14 (not_14_out, s2);
  not not_15 (not_15_out, s1);
  not not_16 (not_16_out, s0);
  not not_17 (not_17_out, s2);
  not not_18 (not_18_out, b2_short);
  not not_19 (not_19_out, s1);
  not not_20 (not_20_out, b2_short);
  not not_21 (not_21_out, s2);
  not not_22 (not_22_out, s0);
  not not_23 (not_23_out, s1);
  not not_24 (not_24_out, s0);
  not not_25 (not_25_out, s2);
  not not_26 (not_26_out, s1);
  not not_27 (not_27_out, s2);
  not not_28 (not_28_out, s0);
  not not_29 (not_29_out, s2);
  not not_30 (not_30_out, s1);
  not not_31 (not_31_out, s0);
  not not_32 (not_32_out, s1);
  not not_33 (not_33_out, s0);
  and and_1 (and_1_out, not_1_out, s1, s0, b2_short);
  and and_2 (and_2_out, s2, not_2_out, not_3_out);
  and and_3 (and_3_out, s2, not_4_out, not_5_out);
  and and_4 (and_4_out, s2, not_6_out, b2_short);
  and and_5 (and_5_out, not_7_out, s0, b2_short);
  and and_6 (and_6_out, not_8_out, s1, not_9_out);
  and and_7 (and_7_out, not_10_out, s1, not_11_out);
  and and_8 (and_8_out, s1, not_12_out, not_13_out);
  and and_9 (and_9_out, not_14_out, not_15_out, not_16_out, b1_long);
  and and_10 (and_10_out, not_17_out, s0, not_18_out);
  and and_11 (and_11_out, not_19_out, s0, not_20_out);
  and and_12 (and_12_out, not_21_out, s1, not_22_out, b2_short);
  and and_13 (and_13_out, s2, not_23_out, not_24_out, b2_short);
  and and_14 (set_ten_hour, not_25_out, not_26_out, s0);
  and and_15 (set_hour, not_27_out, s1, not_28_out);
  and and_16 (set_ten_min, not_29_out, s1, s0);
  and and_17 (set_min, s2, not_30_out, not_31_out);
  and and_18 (set_ten_sec, s2, not_32_out, s0);
  and and_19 (set_sec, s2, s1, not_33_out);
  or or_1 (s2_2b948b35, and_1_out, and_2_out, and_3_out, and_4_out);
  or or_2 (s1_2101c0e9, and_5_out, and_6_out, and_7_out, and_8_out);
  or or_3 (s0_21d125c7, and_9_out, and_10_out, and_11_out, and_12_out, and_13_out);
endmodule

module state3_stopwatch (
  input  b1_short,
  input  b2_short,
  input  dipswitch_1,
  input  clk_100th,
  input  reset,
  output [6:0] x7_0,
  output [6:0] x7_1,
  output [6:0] x7_2,
  output [6:0] x7_3,
  output [6:0] x7_4,
  output [6:0] x7_5
);

  wire and_1_out, and_2_out, d_ff_1_q, not_1_out, not_2_out, stopwatch_logic_1_reset,
       stopwatch_logic_1_run_clk, stopwatch_logic_1_state_new;

  not not_1 (not_1_out, dipswitch_1);
  and and_1 (and_1_out, not_1_out, b1_short);
  and and_2 (and_2_out, b2_short, not_1_out);
  state3_stopwatch_logic stopwatch_logic_1 (
    .state(d_ff_1_q), .b1_short(and_1_out), .b2_short(and_2_out), .state_new(stopwatch_logic_1_state_new),
    .reset(stopwatch_logic_1_reset), .run_clk(stopwatch_logic_1_run_clk));
  D_Flip_Flop d_ff_1 (
    .D(stopwatch_logic_1_state_new), .clk(clk_100th), .Q(d_ff_1_q), .reset(reset));  // open: Qn, preset
  not not_2 (not_2_out, stopwatch_logic_1_run_clk);
  clock24h_display clock24h_display_1 (
    .reset(stopwatch_logic_1_reset), .b1_long(1'b0), .dip_switch(1'b0), .clk_100ths(clk_100th),
    .b1_short(1'b0), .b2_short(1'b0), .timezone(2'b00), .pause(not_2_out), .countdown(1'b0), .x7_0(x7_0),
    .x7_1(x7_1), .x7_2(x7_2), .x7_3(x7_3), .x7_4(x7_4), .x7_5(x7_5));  // open: x7_6, x7_7, set_on
endmodule

module state3_stopwatch_logic (
  input  state,
  input  b1_short,
  input  b2_short,
  output state_new,
  output reset,
  output run_clk
);

  wire and_1_out, and_2_out, and_4_out, and_5_out, not_1_out, not_2_out, not_3_out, not_4_out, not_5_out,
       not_6_out, not_7_out, not_8_out;

  not not_1 (not_1_out, state);
  and and_1 (and_1_out, not_1_out, b1_short, not_2_out);
  not not_2 (not_2_out, b2_short);
  and and_2 (and_2_out, state, not_3_out, not_4_out);
  not not_3 (not_3_out, b1_short);
  not not_4 (not_4_out, b2_short);
  not not_5 (not_5_out, state);
  and and_3 (reset, not_5_out, b2_short);
  not not_6 (not_6_out, state);
  and and_4 (and_4_out, not_6_out, b1_short);
  and and_5 (and_5_out, state, not_7_out, not_8_out);
  not not_7 (not_7_out, b1_short);
  not not_8 (not_8_out, b2_short);
  or or_1 (state_new, and_1_out, and_2_out);
  or or_2 (run_clk, and_4_out, and_5_out);
endmodule

module state4_countdown (
  input  b1_long,
  input  dip_switch,
  input  b1_short,
  input  b2_short,
  input  b2_long,
  input  clk_100th,
  input  reset,
  output [6:0] x7_2,
  output [6:0] x7_3,
  output [6:0] x7_4,
  output [6:0] x7_5,
  output [6:0] x7_6,
  output [6:0] x7_7
);

  wire alarmclock_interrupter_1_alarm, and_1_out, and_2_out, clock24h_display_1_set_on, d_ff_1_q, d_ff_2_q,
       not_1_out, not_2_out, not_3_out, not_4_out, or_1_out, or_2_out, state1_switch_state_machine_1_b0,
       state1_switch_state_machine_1_b1, state1_switch_state_machine_1_set_on;

  not not_1 (not_1_out, dip_switch);
  not not_2 (not_2_out, clock24h_display_1_set_on);
  and and_1 (and_1_out, not_1_out, not_2_out, b1_short);
  or or_1 (or_1_out, and_2_out, reset);
  and and_2 (and_2_out, b2_long, not_2_out, not_1_out);
  not not_3 (not_3_out, state1_switch_state_machine_1_set_on);
  state1_switch_state_machine state1_switch_state_machine_1 (
    .state_b1(d_ff_1_q), .state_b0(d_ff_2_q), .in_e8f0e200(and_1_out), .b1(state1_switch_state_machine_1_b1),
    .b0(state1_switch_state_machine_1_b0), .set_on(state1_switch_state_machine_1_set_on));
  D_Flip_Flop d_ff_1 (
    .D(state1_switch_state_machine_1_b1), .clk(clk_100th), .Q(d_ff_1_q), .reset(or_2_out));  // open: Qn, preset
  D_Flip_Flop d_ff_2 (
    .D(state1_switch_state_machine_1_b0), .clk(clk_100th), .Q(d_ff_2_q), .reset(or_2_out));  // open: Qn, preset
  or or_2 (or_2_out, alarmclock_interrupter_1_alarm, clock24h_display_1_set_on, reset);
  clock24h_display clock24h_display_1 (
    .reset(or_1_out), .b1_long(b1_long), .dip_switch(dip_switch), .clk_100ths(clk_100th),
    .b1_short(b1_short), .b2_short(b2_short), .timezone(2'b00), .pause(not_3_out), .countdown(1'b1),
    .x7_2(x7_2), .x7_3(x7_3), .x7_4(x7_4), .x7_5(x7_5), .x7_6(x7_6), .x7_7(x7_7),
    .set_on(clock24h_display_1_set_on));  // open: x7_0, x7_1
  not not_4 (not_4_out, clock24h_display_1_set_on);
  time_comparator alarmclock_interrupter_1 (
    .alarm_s1(7'b0111111), .alarm_s2(7'b0111111), .alarm_m1(7'b0111111), .alarm_m2(7'b0111111),
    .alarm_h1(7'b0111111), .alarm_h2(7'b0111111), .clock_s1(x7_2), .clock_s2(x7_3), .clock_m1(x7_4),
    .clock_m2(x7_5), .clock_h1(x7_6), .clock_h2(x7_7), .alarm_on(not_4_out),
    .alarm(alarmclock_interrupter_1_alarm));

  // Notes on the sheet:
  //   countdown on
endmodule

module state5_game (
  input  reset,
  input  b1_short,
  input  b2_short,
  input  b1_long,
  input  ds1,
  input  clk,
  output [6:0] Output_bus_1,
  output [6:0] Output_bus_2,
  output [6:0] Output_bus_3,
  output [6:0] Output_bus_4,
  output led
);

  wire and_1_out, and_2_out, and_3_out, and_4_out, and_5_out, counter_1_carry, d_ff_1_q, d_ff_4_q, or_1_out,
       or_2_out, or_3_out, or_4_out, state5_game_statemachine_1_b0_989cf675,
       state5_game_statemachine_1_b1_7f0142b3, state5_game_statemachine_1_counter,
       state5_game_statemachine_1_create_random;
  wire [1:0] d_ff_2_q;
  wire [6:0] clock24h_display_1_x7_0, clock24h_display_1_x7_1, clock24h_display_1_x7_2,
       clock24h_display_1_x7_3;
  wire [11:0] random_1_out;

  and and_1 (and_1_out, ~ds1, b1_short);  // AND_Gate
  and and_2 (and_2_out, ~ds1, b2_short);  // AND_Gate
  and and_3 (and_3_out, ~ds1, b1_long);  // AND_Gate
  or or_1 (or_1_out, counter_1_carry, d_ff_1_q);
  D_Flip_Flop d_ff_1 (.D(counter_1_carry), .clk(clk), .Q(d_ff_1_q));  // open: Qn, preset, reset
  state5_game_statemachine state5_game_statemachine_1 (
    .b0(d_ff_2_q[0]), .b1(d_ff_2_q[1]), .b1_short(and_1_out), .b2_short(and_2_out), .trigger(or_1_out),
    .b1_long(and_3_out), .b0_989cf675(state5_game_statemachine_1_b0_989cf675),
    .b1_7f0142b3(state5_game_statemachine_1_b1_7f0142b3),
    .create_random(state5_game_statemachine_1_create_random), .counter(state5_game_statemachine_1_counter));
  D_Flip_Flop d_ff_2 (
    .D(state5_game_statemachine_1_b0_989cf675), .clk(clk), .Q(d_ff_2_q[0]), .reset(or_2_out));  // open: Qn, preset
  D_Flip_Flop d_ff_3 (
    .D(state5_game_statemachine_1_b1_7f0142b3), .clk(clk), .Q(d_ff_2_q[1]), .reset(or_2_out));  // open: Qn, preset
  or or_2 (or_2_out, ds1, reset);
  D_Flip_Flop d_ff_4 (
    .D(state5_game_statemachine_1_create_random), .clk(clk), .Q(d_ff_4_q));  // open: Qn, preset, reset
  Random #(.width(12)) random_1 (
    .clr(1'b0), .next(state5_game_statemachine_1_create_random), .clk(clk), .out(random_1_out));
  and and_4 (and_4_out, d_ff_2_q[1], d_ff_2_q[0]);
  and and_5 (and_5_out, d_ff_2_q[1], d_ff_2_q[0]);
  or or_3 (or_3_out, and_4_out, or_2_out);
  or or_4 (or_4_out, or_2_out, ~state5_game_statemachine_1_counter);  // OR_Gate
  Counter #(.width(12), .max('hfff)) counter_1 (
    .clr(or_4_out), .load(d_ff_4_q), .up(1'b1), .clk(clk), .D(random_1_out), .carry(counter_1_carry));  // open: count, Q
  D_Flip_Flop d_ff_5 (.D(led), .clk(clk), .Q(led), .preset(counter_1_carry), .reset(or_3_out));  // open: Qn
  clock24h_display clock24h_display_1 (
    .reset(counter_1_carry), .b1_long(1'b0), .dip_switch(1'b0), .clk_100ths(clk), .b1_short(1'b0),
    .b2_short(1'b0), .timezone(2'b00), .pause(and_5_out), .countdown(1'b0), .x7_0(clock24h_display_1_x7_0),
    .x7_1(clock24h_display_1_x7_1), .x7_2(clock24h_display_1_x7_2), .x7_3(clock24h_display_1_x7_3));  // open: x7_4, x7_5, x7_6, x7_7, set_on
  Multiplexer #(.select(2), .width(7), .enable("false")) multiplexer_1 (
    .in0(7'b1101110), .in1(7'b1000000), .in2(7'b1000000), .in3(clock24h_display_1_x7_0), .out(Output_bus_1),
    .sel(d_ff_2_q));
  Multiplexer #(.select(2), .width(7), .enable("false")) multiplexer_2 (
    .in0(7'b1110111), .in1(7'b1000000), .in2(7'b1000000), .in3(clock24h_display_1_x7_1), .out(Output_bus_2),
    .sel(d_ff_2_q));
  Multiplexer #(.select(2), .width(7), .enable("false")) multiplexer_3 (
    .in0(7'b0111000), .in1(7'b1000000), .in2(7'b1000000), .in3(clock24h_display_1_x7_2), .out(Output_bus_3),
    .sel(d_ff_2_q));
  Multiplexer #(.select(2), .width(7), .enable("false")) multiplexer_4 (
    .in0(7'b1110011), .in1(7'b1000000), .in2(7'b1000000), .in3(clock24h_display_1_x7_3), .out(Output_bus_4),
    .sel(d_ff_2_q));
endmodule

module state5_game_statemachine (
  input  b0,
  input  b1,
  input  b1_short,
  input  b2_short,
  input  trigger,
  input  b1_long,
  output b0_989cf675,
  output b1_7f0142b3,
  output create_random,
  output counter
);

  wire and_1_out, and_2_out, and_3_out, and_4_out, and_5_out, and_6_out, and_7_out, and_8_out, and_9_out,
       and_10_out, and_11_out, and_12_out, and_13_out, not_1_out, not_2_out, not_3_out, not_4_out, not_5_out,
       not_6_out, not_7_out, not_8_out, not_9_out, not_10_out, not_11_out, not_12_out, not_13_out,
       not_14_out, not_15_out, not_16_out, not_17_out, not_18_out, not_19_out, not_20_out, not_21_out,
       not_22_out;

  not not_1 (not_1_out, b0);
  not not_2 (not_2_out, b0);
  not not_3 (not_3_out, b1);
  not not_4 (not_4_out, b2_short);
  not not_5 (not_5_out, b2_short);
  not not_6 (not_6_out, b1_long);
  not not_7 (not_7_out, b2_short);
  not not_8 (not_8_out, b1);
  not not_9 (not_9_out, b2_short);
  not not_10 (not_10_out, b1);
  not not_11 (not_11_out, b2_short);
  not not_12 (not_12_out, b2_short);
  not not_13 (not_13_out, trigger);
  not not_14 (not_14_out, b1);
  not not_15 (not_15_out, b2_short);
  not not_16 (not_16_out, b0);
  not not_17 (not_17_out, b1);
  not not_18 (not_18_out, b2_short);
  not not_19 (not_19_out, b1_short);
  not not_20 (not_20_out, b2_short);
  not not_21 (not_21_out, trigger);
  not not_22 (not_22_out, b0);
  and and_1 (and_1_out, not_1_out, b1, trigger);
  and and_2 (and_2_out, not_2_out, b1, b1_short, b2_short);
  and and_3 (and_3_out, b0, not_3_out, not_4_out);
  and and_4 (and_4_out, b0, not_5_out, not_6_out);
  and and_5 (and_5_out, b0, not_7_out, trigger);
  and and_6 (and_6_out, b0, not_8_out, b1_short);
  and and_7 (and_7_out, b0, b1_short, not_9_out);
  and and_8 (and_8_out, not_10_out, b1_short, not_11_out);
  and and_9 (and_9_out, b1, not_12_out, not_13_out);
  and and_10 (and_10_out, b0, not_14_out, b1_short);
  and and_11 (and_11_out, b0, b1, not_15_out);
  and and_12 (and_12_out, not_16_out, not_17_out, b1_short, not_18_out);
  and and_13 (and_13_out, b0, b1, not_19_out, not_20_out, not_21_out, b1_long);
  and and_14 (counter, not_22_out, b1);
  or or_1 (b0_989cf675, and_1_out, and_2_out, and_3_out, and_4_out, and_5_out, and_6_out, and_7_out);
  or or_2 (b1_7f0142b3, and_8_out, and_9_out, and_10_out, and_11_out);
  or or_3 (create_random, and_12_out, and_13_out);
endmodule

module state6_piano (
  input  ds1,
  input  [2:0] current_state,
  input  [6:0] ds2to7,
  output high1,
  output high2,
  output [6:0] x7_0,
  output [6:0] x7_1,
  output [6:0] x7_2,
  output [6:0] x7_3,
  output [6:0] x7_4
);

  wire and_1_out, comparator_1_eq, piano_statemachine_1_e2, piano_statemachine_1_e3, piano_statemachine_1_e4,
       piano_statemachine_1_e5, piano_statemachine_1_e6, piano_statemachine_1_e7, piano_statemachine_1_e8;
  wire [3:0] piano_statemachine_1_n0, piano_statemachine_2_n0;
  wire [6:0] multiplexer_1_out;

  Comparator #(.width(3)) comparator_1 (.a(current_state), .b(3'b110), .eq(comparator_1_eq));  // open: gt, lt
  Multiplexer #(.width(7), .enable("false")) multiplexer_1 (
    .in0({7{1'b0}}), .in1(ds2to7), .out(multiplexer_1_out), .sel(and_1_out));
  and and_1 (and_1_out, ~ds1, comparator_1_eq);  // AND_Gate
  state6_piano_statemachine piano_statemachine_1 (
    .ds2(multiplexer_1_out[0]), .ds3(multiplexer_1_out[1]), .ds4(multiplexer_1_out[2]),
    .ds5(multiplexer_1_out[3]), .ds6(multiplexer_1_out[4]), .ds7(multiplexer_1_out[5]),
    .ds8(multiplexer_1_out[6]), .n3(piano_statemachine_1_n0[3]), .n2(piano_statemachine_1_n0[2]),
    .n1(piano_statemachine_1_n0[1]), .n0(piano_statemachine_1_n0[0]), .e2(piano_statemachine_1_e2),
    .e3(piano_statemachine_1_e3), .e4(piano_statemachine_1_e4), .e5(piano_statemachine_1_e5),
    .e6(piano_statemachine_1_e6), .e7(piano_statemachine_1_e7), .e8(piano_statemachine_1_e8));
  state6_piano_statemachine piano_statemachine_2 (
    .ds2(piano_statemachine_1_e2), .ds3(piano_statemachine_1_e3), .ds4(piano_statemachine_1_e4),
    .ds5(piano_statemachine_1_e5), .ds6(piano_statemachine_1_e6), .ds7(piano_statemachine_1_e7),
    .ds8(piano_statemachine_1_e8), .n3(piano_statemachine_2_n0[3]), .n2(piano_statemachine_2_n0[2]),
    .n1(piano_statemachine_2_n0[1]), .n0(piano_statemachine_2_n0[0]));  // open: e2, e3, e4, e5, e6, e7, e8
  frequency_generator frequency_generator_1 (.note(piano_statemachine_1_n0), .high(high1));
  frequency_generator frequency_generator_2 (.note(piano_statemachine_2_n0), .high(high2));

  assign x7_0 = 7'b1011100;
  assign x7_1 = 7'b1010100;
  assign x7_2 = 7'b1110111;
  assign x7_3 = 7'b0000110;
  assign x7_4 = 7'b1110011;

  // Notes on the sheet:
  //   O
  //   N
  //   A
  //   I
  //   P
endmodule
module state6_piano_statemachine (
  input  ds2,
  input  ds3,
  input  ds4,
  input  ds5,
  input  ds6,
  input  ds7,
  input  ds8,
  output n3,
  output n2,
  output n1,
  output n0,
  output e2,
  output e3,
  output e4,
  output e5,
  output e6,
  output e7,
  output e8
);

  wire and_1_out, and_2_out, and_3_out, and_4_out, and_5_out, and_6_out, and_7_out, and_8_out, and_9_out,
       and_10_out, and_11_out, and_12_out, and_13_out, and_14_out, and_15_out, and_16_out, and_17_out,
       and_18_out, and_19_out, and_20_out, and_21_out, and_22_out, and_23_out, and_24_out, and_25_out,
       and_26_out, and_27_out, and_28_out, and_29_out, and_30_out, and_31_out, and_32_out, and_33_out,
       and_34_out, and_35_out, and_36_out, and_37_out, and_39_out, and_40_out, and_41_out, and_42_out,
       and_43_out, and_44_out, and_45_out, and_46_out, and_47_out, and_48_out, and_49_out, and_50_out,
       and_51_out, and_52_out, and_53_out, and_54_out, and_55_out, and_56_out, and_57_out, and_58_out,
       not_1_out, not_2_out, not_3_out, not_4_out, not_5_out, not_6_out, not_7_out, not_8_out, not_9_out,
       not_10_out, not_11_out, not_12_out, not_13_out, not_14_out, not_15_out, not_16_out, not_17_out,
       not_18_out, not_19_out, not_20_out, not_21_out, not_22_out, not_23_out, not_24_out, not_25_out,
       not_26_out, not_27_out, not_28_out, not_29_out, not_30_out, not_31_out, not_32_out, not_33_out,
       not_34_out, not_35_out, not_36_out, not_37_out, not_38_out, not_39_out, not_40_out, not_41_out,
       not_42_out, not_43_out, not_44_out, not_45_out, not_46_out, not_47_out, not_48_out, not_49_out,
       not_50_out, not_51_out, not_52_out, not_53_out, not_54_out, not_55_out, not_56_out, not_57_out,
       not_58_out, not_59_out, not_60_out, not_61_out, not_62_out, not_63_out, not_64_out, not_65_out,
       not_66_out, not_67_out, not_68_out, not_69_out, not_70_out, not_71_out, not_72_out, not_73_out,
       not_74_out, not_75_out, not_76_out, not_77_out, not_78_out, not_79_out, not_80_out, not_81_out,
       not_82_out, not_83_out, not_84_out, not_85_out, not_86_out, not_87_out, not_88_out, not_89_out,
       not_90_out, not_91_out, not_92_out, not_93_out, not_94_out, not_95_out, not_96_out, not_97_out,
       not_98_out, not_99_out, not_100_out, not_101_out, not_102_out, not_103_out, not_104_out, not_105_out,
       not_106_out, not_107_out, not_108_out, not_109_out, not_110_out, not_111_out, not_112_out,
       not_113_out, not_114_out, not_115_out, not_116_out, not_117_out, not_118_out, not_119_out,
       not_120_out, not_121_out, not_122_out, not_123_out, not_124_out, not_125_out, not_126_out,
       not_127_out, not_128_out, not_129_out, not_130_out, not_131_out, not_132_out, not_133_out,
       not_134_out, not_135_out, not_136_out, not_137_out, not_138_out, not_139_out, not_140_out,
       not_141_out, not_142_out, not_143_out, not_144_out, not_145_out, not_146_out, not_147_out,
       not_148_out, not_149_out, not_150_out, not_151_out, not_152_out, not_153_out, not_154_out,
       not_155_out, not_156_out, not_157_out, not_158_out, not_159_out, not_160_out, not_161_out,
       not_162_out, not_163_out, not_164_out, not_165_out, not_166_out, not_167_out, not_168_out,
       not_169_out, not_170_out, not_171_out, not_172_out, not_173_out, not_174_out, not_175_out,
       not_176_out, not_177_out, not_178_out, not_179_out, not_180_out, not_181_out, not_182_out,
       not_183_out, not_184_out, not_185_out, not_186_out, not_187_out, not_188_out, not_189_out,
       not_190_out, not_191_out, not_192_out, not_193_out, not_194_out, not_195_out, not_196_out,
       not_197_out, not_198_out, not_199_out, not_200_out, not_201_out, not_202_out, not_203_out,
       not_204_out, not_205_out, not_206_out, not_207_out, not_208_out, not_209_out, not_210_out,
       not_211_out, not_212_out, not_213_out, not_214_out, not_215_out, not_216_out, not_217_out,
       not_218_out, not_219_out, not_220_out, not_221_out, not_222_out, not_223_out, not_224_out,
       not_225_out, not_226_out, not_227_out, not_228_out, not_229_out, not_230_out, not_231_out,
       not_232_out, not_233_out, not_234_out, not_235_out, not_236_out, not_237_out, not_238_out,
       not_239_out, not_240_out, not_241_out, not_242_out, not_243_out, not_244_out, not_245_out,
       not_246_out, not_247_out, not_248_out, not_249_out, not_250_out, not_251_out, not_252_out,
       not_253_out, not_254_out, not_255_out, not_256_out, not_257_out, not_258_out, not_259_out,
       not_260_out, not_261_out, not_262_out, not_263_out, not_264_out, not_265_out, not_266_out,
       not_267_out, not_268_out, not_269_out, not_270_out, not_271_out, not_272_out, not_273_out,
       not_274_out, not_275_out, not_276_out, not_277_out, not_278_out, not_279_out, not_280_out,
       not_281_out, not_282_out, not_283_out, not_284_out, not_285_out, not_286_out, not_287_out,
       not_288_out, not_289_out, not_290_out;

  not not_1 (not_1_out, ds2);
  not not_2 (not_2_out, ds3);
  not not_3 (not_3_out, ds4);
  not not_4 (not_4_out, ds5);
  not not_5 (not_5_out, ds6);
  not not_6 (not_6_out, ds2);
  not not_7 (not_7_out, ds3);
  not not_8 (not_8_out, ds4);
  not not_9 (not_9_out, ds5);
  not not_10 (not_10_out, ds6);
  not not_11 (not_11_out, ds2);
  not not_12 (not_12_out, ds3);
  not not_13 (not_13_out, ds4);
  not not_14 (not_14_out, ds5);
  not not_15 (not_15_out, ds7);
  not not_16 (not_16_out, ds2);
  not not_17 (not_17_out, ds3);
  not not_18 (not_18_out, ds4);
  not not_19 (not_19_out, ds5);
  not not_20 (not_20_out, ds8);
  not not_21 (not_21_out, ds2);
  not not_22 (not_22_out, ds3);
  not not_23 (not_23_out, ds4);
  not not_24 (not_24_out, ds6);
  not not_25 (not_25_out, ds7);
  not not_26 (not_26_out, ds2);
  not not_27 (not_27_out, ds3);
  not not_28 (not_28_out, ds4);
  not not_29 (not_29_out, ds6);
  not not_30 (not_30_out, ds8);
  not not_31 (not_31_out, ds2);
  not not_32 (not_32_out, ds3);
  not not_33 (not_33_out, ds4);
  not not_34 (not_34_out, ds7);
  not not_35 (not_35_out, ds8);
  not not_36 (not_36_out, ds2);
  not not_37 (not_37_out, ds3);
  not not_38 (not_38_out, ds5);
  not not_39 (not_39_out, ds6);
  not not_40 (not_40_out, ds7);
  not not_41 (not_41_out, ds2);
  not not_42 (not_42_out, ds3);
  not not_43 (not_43_out, ds5);
  not not_44 (not_44_out, ds6);
  not not_45 (not_45_out, ds8);
  not not_46 (not_46_out, ds2);
  not not_47 (not_47_out, ds3);
  not not_48 (not_48_out, ds5);
  not not_49 (not_49_out, ds7);
  not not_50 (not_50_out, ds8);
  not not_51 (not_51_out, ds2);
  not not_52 (not_52_out, ds3);
  not not_53 (not_53_out, ds6);
  not not_54 (not_54_out, ds7);
  not not_55 (not_55_out, ds8);
  not not_56 (not_56_out, ds2);
  not not_57 (not_57_out, ds4);
  not not_58 (not_58_out, ds5);
  not not_59 (not_59_out, ds6);
  not not_60 (not_60_out, ds7);
  not not_61 (not_61_out, ds2);
  not not_62 (not_62_out, ds3);
  not not_63 (not_63_out, ds4);
  not not_64 (not_64_out, ds5);
  not not_65 (not_65_out, ds6);
  not not_66 (not_66_out, ds2);
  not not_67 (not_67_out, ds4);
  not not_68 (not_68_out, ds5);
  not not_69 (not_69_out, ds6);
  not not_70 (not_70_out, ds8);
  not not_71 (not_71_out, ds2);
  not not_72 (not_72_out, ds4);
  not not_73 (not_73_out, ds5);
  not not_74 (not_74_out, ds7);
  not not_75 (not_75_out, ds8);
  not not_76 (not_76_out, ds2);
  not not_77 (not_77_out, ds4);
  not not_78 (not_78_out, ds6);
  not not_79 (not_79_out, ds7);
  not not_80 (not_80_out, ds8);
  not not_81 (not_81_out, ds2);
  not not_82 (not_82_out, ds5);
  not not_83 (not_83_out, ds6);
  not not_84 (not_84_out, ds7);
  not not_85 (not_85_out, ds8);
  not not_86 (not_86_out, ds3);
  not not_87 (not_87_out, ds4);
  not not_88 (not_88_out, ds5);
  not not_89 (not_89_out, ds6);
  not not_90 (not_90_out, ds7);
  not not_91 (not_91_out, ds3);
  not not_92 (not_92_out, ds4);
  not not_93 (not_93_out, ds5);
  not not_94 (not_94_out, ds6);
  not not_95 (not_95_out, ds8);
  not not_96 (not_96_out, ds3);
  not not_97 (not_97_out, ds4);
  not not_98 (not_98_out, ds5);
  not not_99 (not_99_out, ds7);
  not not_100 (not_100_out, ds8);
  not not_101 (not_101_out, ds3);
  not not_102 (not_102_out, ds4);
  not not_103 (not_103_out, ds6);
  not not_104 (not_104_out, ds7);
  not not_105 (not_105_out, ds8);
  not not_106 (not_106_out, ds3);
  not not_107 (not_107_out, ds5);
  not not_108 (not_108_out, ds6);
  not not_109 (not_109_out, ds7);
  not not_110 (not_110_out, ds8);
  not not_111 (not_111_out, ds4);
  not not_112 (not_112_out, ds5);
  not not_113 (not_113_out, ds6);
  not not_114 (not_114_out, ds7);
  not not_115 (not_115_out, ds8);
  not not_116 (not_116_out, ds2);
  not not_117 (not_117_out, ds4);
  not not_118 (not_118_out, ds5);
  not not_119 (not_119_out, ds6);
  not not_120 (not_120_out, ds7);
  not not_121 (not_121_out, ds2);
  not not_122 (not_122_out, ds3);
  not not_123 (not_123_out, ds4);
  not not_124 (not_124_out, ds5);
  not not_125 (not_125_out, ds7);
  not not_126 (not_126_out, ds2);
  not not_127 (not_127_out, ds3);
  not not_128 (not_128_out, ds4);
  not not_129 (not_129_out, ds5);
  not not_130 (not_130_out, ds8);
  not not_131 (not_131_out, ds2);
  not not_132 (not_132_out, ds4);
  not not_133 (not_133_out, ds5);
  not not_134 (not_134_out, ds6);
  not not_135 (not_135_out, ds8);
  not not_136 (not_136_out, ds2);
  not not_137 (not_137_out, ds4);
  not not_138 (not_138_out, ds5);
  not not_139 (not_139_out, ds7);
  not not_140 (not_140_out, ds8);
  not not_141 (not_141_out, ds2);
  not not_142 (not_142_out, ds4);
  not not_143 (not_143_out, ds6);
  not not_144 (not_144_out, ds7);
  not not_145 (not_145_out, ds8);
  not not_146 (not_146_out, ds2);
  not not_147 (not_147_out, ds5);
  not not_148 (not_148_out, ds6);
  not not_149 (not_149_out, ds7);
  not not_150 (not_150_out, ds8);
  not not_151 (not_151_out, ds2);
  not not_152 (not_152_out, ds3);
  not not_153 (not_153_out, ds4);
  not not_154 (not_154_out, ds5);
  not not_155 (not_155_out, ds6);
  not not_156 (not_156_out, ds2);
  not not_157 (not_157_out, ds3);
  not not_158 (not_158_out, ds4);
  not not_159 (not_159_out, ds5);
  not not_160 (not_160_out, ds6);
  not not_161 (not_161_out, ds2);
  not not_162 (not_162_out, ds3);
  not not_163 (not_163_out, ds4);
  not not_164 (not_164_out, ds5);
  not not_165 (not_165_out, ds7);
  not not_166 (not_166_out, ds2);
  not not_167 (not_167_out, ds3);
  not not_168 (not_168_out, ds4);
  not not_169 (not_169_out, ds5);
  not not_170 (not_170_out, ds8);
  not not_171 (not_171_out, ds2);
  not not_172 (not_172_out, ds3);
  not not_173 (not_173_out, ds4);
  not not_174 (not_174_out, ds6);
  not not_175 (not_175_out, ds7);
  not not_176 (not_176_out, ds2);
  not not_177 (not_177_out, ds3);
  not not_178 (not_178_out, ds4);
  not not_179 (not_179_out, ds6);
  not not_180 (not_180_out, ds8);
  not not_181 (not_181_out, ds2);
  not not_182 (not_182_out, ds3);
  not not_183 (not_183_out, ds4);
  not not_184 (not_184_out, ds7);
  not not_185 (not_185_out, ds8);
  not not_186 (not_186_out, ds4);
  not not_187 (not_187_out, ds5);
  not not_188 (not_188_out, ds6);
  not not_189 (not_189_out, ds7);
  not not_190 (not_190_out, ds8);
  not not_191 (not_191_out, ds2);
  not not_192 (not_192_out, ds5);
  not not_193 (not_193_out, ds6);
  not not_194 (not_194_out, ds7);
  not not_195 (not_195_out, ds8);
  not not_196 (not_196_out, ds3);
  not not_197 (not_197_out, ds5);
  not not_198 (not_198_out, ds6);
  not not_199 (not_199_out, ds7);
  not not_200 (not_200_out, ds8);
  not not_201 (not_201_out, ds2);
  not not_202 (not_202_out, ds3);
  not not_203 (not_203_out, ds6);
  not not_204 (not_204_out, ds7);
  not not_205 (not_205_out, ds8);
  not not_206 (not_206_out, ds2);
  not not_207 (not_207_out, ds4);
  not not_208 (not_208_out, ds6);
  not not_209 (not_209_out, ds7);
  not not_210 (not_210_out, ds8);
  not not_211 (not_211_out, ds3);
  not not_212 (not_212_out, ds4);
  not not_213 (not_213_out, ds6);
  not not_214 (not_214_out, ds7);
  not not_215 (not_215_out, ds8);
  not not_216 (not_216_out, ds2);
  not not_217 (not_217_out, ds3);
  not not_218 (not_218_out, ds4);
  not not_219 (not_219_out, ds7);
  not not_220 (not_220_out, ds8);
  not not_221 (not_221_out, ds2);
  not not_222 (not_222_out, ds3);
  not not_223 (not_223_out, ds5);
  not not_224 (not_224_out, ds7);
  not not_225 (not_225_out, ds8);
  not not_226 (not_226_out, ds2);
  not not_227 (not_227_out, ds4);
  not not_228 (not_228_out, ds5);
  not not_229 (not_229_out, ds7);
  not not_230 (not_230_out, ds8);
  not not_231 (not_231_out, ds3);
  not not_232 (not_232_out, ds4);
  not not_233 (not_233_out, ds5);
  not not_234 (not_234_out, ds7);
  not not_235 (not_235_out, ds8);
  not not_236 (not_236_out, ds2);
  not not_237 (not_237_out, ds3);
  not not_238 (not_238_out, ds4);
  not not_239 (not_239_out, ds5);
  not not_240 (not_240_out, ds8);
  not not_241 (not_241_out, ds2);
  not not_242 (not_242_out, ds3);
  not not_243 (not_243_out, ds4);
  not not_244 (not_244_out, ds6);
  not not_245 (not_245_out, ds8);
  not not_246 (not_246_out, ds2);
  not not_247 (not_247_out, ds3);
  not not_248 (not_248_out, ds5);
  not not_249 (not_249_out, ds6);
  not not_250 (not_250_out, ds8);
  not not_251 (not_251_out, ds2);
  not not_252 (not_252_out, ds4);
  not not_253 (not_253_out, ds5);
  not not_254 (not_254_out, ds6);
  not not_255 (not_255_out, ds8);
  not not_256 (not_256_out, ds3);
  not not_257 (not_257_out, ds4);
  not not_258 (not_258_out, ds5);
  not not_259 (not_259_out, ds6);
  not not_260 (not_260_out, ds8);
  not not_261 (not_261_out, ds2);
  not not_262 (not_262_out, ds3);
  not not_263 (not_263_out, ds4);
  not not_264 (not_264_out, ds5);
  not not_265 (not_265_out, ds6);
  not not_266 (not_266_out, ds2);
  not not_267 (not_267_out, ds3);
  not not_268 (not_268_out, ds4);
  not not_269 (not_269_out, ds5);
  not not_270 (not_270_out, ds7);
  not not_271 (not_271_out, ds2);
  not not_272 (not_272_out, ds3);
  not not_273 (not_273_out, ds4);
  not not_274 (not_274_out, ds6);
  not not_275 (not_275_out, ds7);
  not not_276 (not_276_out, ds2);
  not not_277 (not_277_out, ds3);
  not not_278 (not_278_out, ds5);
  not not_279 (not_279_out, ds6);
  not not_280 (not_280_out, ds7);
  not not_281 (not_281_out, ds2);
  not not_282 (not_282_out, ds4);
  not not_283 (not_283_out, ds5);
  not not_284 (not_284_out, ds6);
  not not_285 (not_285_out, ds7);
  not not_286 (not_286_out, ds3);
  not not_287 (not_287_out, ds4);
  not not_288 (not_288_out, ds5);
  not not_289 (not_289_out, ds6);
  not not_290 (not_290_out, ds7);
  and and_1 (and_1_out, not_1_out, not_2_out, not_3_out, not_4_out, not_5_out, ds8);
  and and_2 (and_2_out, not_6_out, not_7_out, not_8_out, not_9_out, not_10_out, ds7);
  and and_3 (and_3_out, not_11_out, not_12_out, not_13_out, not_14_out, ds6, not_15_out);
  and and_4 (and_4_out, not_16_out, not_17_out, not_18_out, not_19_out, ds6, not_20_out);
  and and_5 (and_5_out, not_21_out, not_22_out, not_23_out, ds5, not_24_out, not_25_out);
  and and_6 (and_6_out, not_26_out, not_27_out, not_28_out, ds5, not_29_out, not_30_out);
  and and_7 (and_7_out, not_31_out, not_32_out, not_33_out, ds5, not_34_out, not_35_out);
  and and_8 (and_8_out, not_36_out, not_37_out, ds4, not_38_out, not_39_out, not_40_out);
  and and_9 (and_9_out, not_41_out, not_42_out, ds4, not_43_out, not_44_out, not_45_out);
  and and_10 (and_10_out, not_46_out, not_47_out, ds4, not_48_out, not_49_out, not_50_out);
  and and_11 (and_11_out, not_51_out, not_52_out, ds4, not_53_out, not_54_out, not_55_out);
  and and_12 (and_12_out, not_56_out, not_57_out, not_58_out, not_59_out, not_60_out, ds8);
  and and_13 (and_13_out, not_61_out, not_62_out, not_63_out, not_64_out, not_65_out, ds7);
  and and_14 (and_14_out, not_66_out, not_67_out, not_68_out, not_69_out, ds7, not_70_out);
  and and_15 (and_15_out, not_71_out, ds3, not_72_out, not_73_out, not_74_out, not_75_out);
  and and_16 (and_16_out, not_76_out, ds3, not_77_out, not_78_out, not_79_out, not_80_out);
  and and_17 (and_17_out, not_81_out, ds3, not_82_out, not_83_out, not_84_out, not_85_out);
  and and_18 (and_18_out, ds2, not_86_out, not_87_out, not_88_out, not_89_out, not_90_out);
  and and_19 (and_19_out, ds2, not_91_out, not_92_out, not_93_out, not_94_out, not_95_out);
  and and_20 (and_20_out, ds2, not_96_out, not_97_out, not_98_out, not_99_out, not_100_out);
  and and_21 (and_21_out, ds2, not_101_out, not_102_out, not_103_out, not_104_out, not_105_out);
  and and_22 (and_22_out, ds2, not_106_out, not_107_out, not_108_out, not_109_out, not_110_out);
  and and_23 (and_23_out, ds2, not_111_out, not_112_out, not_113_out, not_114_out, not_115_out);
  and and_24 (and_24_out, not_116_out, not_117_out, not_118_out, not_119_out, not_120_out, ds8);
  and and_25 (and_25_out, not_121_out, not_122_out, not_123_out, not_124_out, ds6, not_125_out);
  and and_26 (and_26_out, not_126_out, not_127_out, not_128_out, not_129_out, ds6, not_130_out);
  and and_27 (and_27_out, not_131_out, ds3, not_132_out, not_133_out, not_134_out, not_135_out);
  and and_28 (and_28_out, not_136_out, ds3, not_137_out, not_138_out, not_139_out, not_140_out);
  and and_29 (and_29_out, not_141_out, ds3, not_142_out, not_143_out, not_144_out, not_145_out);
  and and_30 (and_30_out, not_146_out, ds3, not_147_out, not_148_out, not_149_out, not_150_out);
  and and_31 (and_31_out, not_151_out, not_152_out, not_153_out, not_154_out, not_155_out, ds8);
  and and_32 (and_32_out, not_156_out, not_157_out, not_158_out, not_159_out, not_160_out, ds7);
  and and_33 (and_33_out, not_161_out, not_162_out, not_163_out, not_164_out, ds6, not_165_out);
  and and_34 (and_34_out, not_166_out, not_167_out, not_168_out, not_169_out, ds6, not_170_out);
  and and_35 (and_35_out, not_171_out, not_172_out, not_173_out, ds5, not_174_out, not_175_out);
  and and_36 (and_36_out, not_176_out, not_177_out, not_178_out, ds5, not_179_out, not_180_out);
  and and_37 (and_37_out, not_181_out, not_182_out, not_183_out, ds5, not_184_out, not_185_out);
  and and_38 (e3, ds2, ds3, not_186_out, not_187_out, not_188_out, not_189_out, not_190_out);
  and and_39 (and_39_out, not_191_out, ds3, ds4, not_192_out, not_193_out, not_194_out, not_195_out);
  and and_40 (and_40_out, ds2, not_196_out, ds4, not_197_out, not_198_out, not_199_out, not_200_out);
  and and_41 (and_41_out, not_201_out, not_202_out, ds4, ds5, not_203_out, not_204_out, not_205_out);
  and and_42 (and_42_out, not_206_out, ds3, not_207_out, ds5, not_208_out, not_209_out, not_210_out);
  and and_43 (and_43_out, ds2, not_211_out, not_212_out, ds5, not_213_out, not_214_out, not_215_out);
  and and_44 (and_44_out, not_216_out, not_217_out, not_218_out, ds5, ds6, not_219_out, not_220_out);
  and and_45 (and_45_out, not_221_out, not_222_out, ds4, not_223_out, ds6, not_224_out, not_225_out);
  and and_46 (and_46_out, not_226_out, ds3, not_227_out, not_228_out, ds6, not_229_out, not_230_out);
  and and_47 (and_47_out, ds2, not_231_out, not_232_out, not_233_out, ds6, not_234_out, not_235_out);
  and and_48 (and_48_out, not_236_out, not_237_out, not_238_out, not_239_out, ds6, ds7, not_240_out);
  and and_49 (and_49_out, not_241_out, not_242_out, not_243_out, ds5, not_244_out, ds7, not_245_out);
  and and_50 (and_50_out, not_246_out, not_247_out, ds4, not_248_out, not_249_out, ds7, not_250_out);
  and and_51 (and_51_out, not_251_out, ds3, not_252_out, not_253_out, not_254_out, ds7, not_255_out);
  and and_52 (and_52_out, ds2, not_256_out, not_257_out, not_258_out, not_259_out, ds7, not_260_out);
  and and_53 (and_53_out, not_261_out, not_262_out, not_263_out, not_264_out, not_265_out, ds7, ds8);
  and and_54 (and_54_out, not_266_out, not_267_out, not_268_out, not_269_out, ds6, not_270_out, ds8);
  and and_55 (and_55_out, not_271_out, not_272_out, not_273_out, ds5, not_274_out, not_275_out, ds8);
  and and_56 (and_56_out, not_276_out, not_277_out, ds4, not_278_out, not_279_out, not_280_out, ds8);
  and and_57 (and_57_out, not_281_out, ds3, not_282_out, not_283_out, not_284_out, not_285_out, ds8);
  and and_58 (and_58_out, ds2, not_286_out, not_287_out, not_288_out, not_289_out, not_290_out, ds8);
  or or_1 (n3, and_1_out, and_2_out, and_3_out, and_4_out, and_5_out, and_6_out, and_7_out, and_8_out, and_9_out, and_10_out, and_11_out);
  or or_2 (n1, and_24_out, and_25_out, and_26_out, and_27_out, and_28_out, and_29_out, and_30_out);
  or or_3 (n0, and_31_out, and_32_out, and_33_out, and_34_out, and_35_out, and_36_out, and_37_out);
  or or_4 (e4, and_39_out, and_40_out);
  or or_5 (e5, and_41_out, and_42_out, and_43_out);
  or or_6 (e6, and_44_out, and_45_out, and_46_out, and_47_out);
  or or_7 (e7, and_48_out, and_49_out, and_50_out, and_51_out, and_52_out);
  or or_8 (e8, and_53_out, and_54_out, and_55_out, and_56_out, and_57_out, and_58_out);
  or or_9 (n2, and_12_out, and_13_out, and_14_out, and_15_out, and_16_out, and_17_out, and_18_out, and_19_out, and_20_out, and_21_out, and_22_out, and_23_out);

  assign e2 = 1'b0;
endmodule

module frequency_generator (
  input  [3:0] note,
  output high
);

  wire clock_1_out, counter_1_carry, counter_2_carry, counter_3_carry, counter_4_carry, counter_5_carry,
       counter_6_carry, counter_7_carry, counter_8_carry, counter_9_carry, counter_10_carry,
       counter_11_carry, counter_12_carry, counter_13_carry, counter_14_carry, counter_15_carry, d_ff_1_q,
       d_ff_2_q, d_ff_3_q, d_ff_4_q, d_ff_5_q, d_ff_6_q, d_ff_7_q, d_ff_8_q, d_ff_9_q, d_ff_10_q, d_ff_11_q,
       d_ff_12_q, d_ff_13_q, d_ff_14_q, d_ff_15_q, gated_clock_preventer_1_output_1,
       gated_clock_preventer_2_output_1, gated_clock_preventer_3_output_1, gated_clock_preventer_4_output_1,
       gated_clock_preventer_5_output_1, gated_clock_preventer_6_output_1, gated_clock_preventer_7_output_1,
       gated_clock_preventer_8_output_1, gated_clock_preventer_9_output_1, gated_clock_preventer_10_output_1,
       gated_clock_preventer_11_output_1, gated_clock_preventer_12_output_1,
       gated_clock_preventer_13_output_1, gated_clock_preventer_14_output_1,
       gated_clock_preventer_15_output_1;

  Clock clock_1 (.out(clock_1_out));
  Counter #(.max('he9)) counter_1 (
    .clr(1'b0), .load(1'b0), .up(1'b1), .clk(clock_1_out), .D({8{1'b0}}), .carry(counter_1_carry));  // open: count, Q
  Counter #(.max('hdc)) counter_2 (
    .clr(1'b0), .load(1'b0), .up(1'b1), .clk(clock_1_out), .D({8{1'b0}}), .carry(counter_2_carry));  // open: count, Q
  Counter #(.max('hcf)) counter_3 (
    .clr(1'b0), .load(1'b0), .up(1'b1), .clk(clock_1_out), .D({8{1'b0}}), .carry(counter_3_carry));  // open: count, Q
  Counter #(.max('hc4)) counter_4 (
    .clr(1'b0), .load(1'b0), .up(1'b1), .clk(clock_1_out), .D({8{1'b0}}), .carry(counter_4_carry));  // open: count, Q
  Counter #(.max('hb9)) counter_5 (
    .clr(1'b0), .load(1'b0), .up(1'b1), .clk(clock_1_out), .D({8{1'b0}}), .carry(counter_5_carry));  // open: count, Q
  Counter #(.max('hae)) counter_6 (
    .clr(1'b0), .load(1'b0), .up(1'b1), .clk(clock_1_out), .D({8{1'b0}}), .carry(counter_6_carry));  // open: count, Q
  Counter #(.max('ha5)) counter_7 (
    .clr(1'b0), .load(1'b0), .up(1'b1), .clk(clock_1_out), .D({8{1'b0}}), .carry(counter_7_carry));  // open: count, Q
  Counter #(.max('h9b)) counter_8 (
    .clr(1'b0), .load(1'b0), .up(1'b1), .clk(clock_1_out), .D({8{1'b0}}), .carry(counter_8_carry));  // open: count, Q
  Counter #(.max('h93)) counter_9 (
    .clr(1'b0), .load(1'b0), .up(1'b1), .clk(clock_1_out), .D({8{1'b0}}), .carry(counter_9_carry));  // open: count, Q
  gated_clock_preventer gated_clock_preventer_1 (
    .input_1(counter_1_carry), .Q(d_ff_1_q), .Output_1(gated_clock_preventer_1_output_1));
  gated_clock_preventer gated_clock_preventer_2 (
    .input_1(counter_2_carry), .Q(d_ff_2_q), .Output_1(gated_clock_preventer_2_output_1));
  gated_clock_preventer gated_clock_preventer_3 (
    .input_1(counter_3_carry), .Q(d_ff_3_q), .Output_1(gated_clock_preventer_3_output_1));
  gated_clock_preventer gated_clock_preventer_4 (
    .input_1(counter_4_carry), .Q(d_ff_4_q), .Output_1(gated_clock_preventer_4_output_1));
  gated_clock_preventer gated_clock_preventer_6 (
    .input_1(counter_5_carry), .Q(d_ff_5_q), .Output_1(gated_clock_preventer_6_output_1));
  gated_clock_preventer gated_clock_preventer_8 (
    .input_1(counter_6_carry), .Q(d_ff_6_q), .Output_1(gated_clock_preventer_8_output_1));
  gated_clock_preventer gated_clock_preventer_11 (
    .input_1(counter_7_carry), .Q(d_ff_7_q), .Output_1(gated_clock_preventer_11_output_1));
  gated_clock_preventer gated_clock_preventer_13 (
    .input_1(counter_8_carry), .Q(d_ff_8_q), .Output_1(gated_clock_preventer_13_output_1));
  gated_clock_preventer gated_clock_preventer_15 (
    .input_1(counter_9_carry), .Q(d_ff_9_q), .Output_1(gated_clock_preventer_15_output_1));
  D_Flip_Flop d_ff_1 (
    .D(gated_clock_preventer_1_output_1), .clk(clock_1_out), .Q(d_ff_1_q), .preset(1'b0), .reset(1'b0));  // open: Qn
  D_Flip_Flop d_ff_2 (
    .D(gated_clock_preventer_2_output_1), .clk(clock_1_out), .Q(d_ff_2_q), .preset(1'b0), .reset(1'b0));  // open: Qn
  D_Flip_Flop d_ff_3 (
    .D(gated_clock_preventer_3_output_1), .clk(clock_1_out), .Q(d_ff_3_q), .preset(1'b0), .reset(1'b0));  // open: Qn
  D_Flip_Flop d_ff_4 (
    .D(gated_clock_preventer_4_output_1), .clk(clock_1_out), .Q(d_ff_4_q), .preset(1'b0), .reset(1'b0));  // open: Qn
  D_Flip_Flop d_ff_5 (
    .D(gated_clock_preventer_6_output_1), .clk(clock_1_out), .Q(d_ff_5_q), .preset(1'b0), .reset(1'b0));  // open: Qn
  D_Flip_Flop d_ff_6 (
    .D(gated_clock_preventer_8_output_1), .clk(clock_1_out), .Q(d_ff_6_q), .preset(1'b0), .reset(1'b0));  // open: Qn
  D_Flip_Flop d_ff_7 (
    .D(gated_clock_preventer_11_output_1), .clk(clock_1_out), .Q(d_ff_7_q), .preset(1'b0), .reset(1'b0));  // open: Qn
  D_Flip_Flop d_ff_8 (
    .D(gated_clock_preventer_13_output_1), .clk(clock_1_out), .Q(d_ff_8_q), .preset(1'b0), .reset(1'b0));  // open: Qn
  D_Flip_Flop d_ff_9 (
    .D(gated_clock_preventer_15_output_1), .clk(clock_1_out), .Q(d_ff_9_q), .preset(1'b0), .reset(1'b0));  // open: Qn
  Multiplexer #(.select(4), .enable("false")) multiplexer_1 (
    .in0(1'b0), .in1(d_ff_1_q), .in2(d_ff_2_q), .in3(d_ff_3_q), .in4(d_ff_4_q), .in5(d_ff_5_q),
    .in6(d_ff_6_q), .in7(d_ff_7_q), .in8(d_ff_8_q), .in9(d_ff_9_q), .in10(d_ff_10_q), .in11(d_ff_11_q),
    .in12(d_ff_12_q), .in13(d_ff_13_q), .in14(d_ff_14_q), .in15(d_ff_15_q), .out(high), .sel(note));
  Counter #(.max('h8a)) counter_10 (
    .clr(1'b0), .load(1'b0), .up(1'b1), .clk(clock_1_out), .D({8{1'b0}}), .carry(counter_10_carry));  // open: count, Q
  Counter #(.max('h83)) counter_11 (
    .clr(1'b0), .load(1'b0), .up(1'b1), .clk(clock_1_out), .D({8{1'b0}}), .carry(counter_11_carry));  // open: count, Q
  Counter #(.max('h80)) counter_12 (
    .clr(1'b0), .load(1'b0), .up(1'b1), .clk(clock_1_out), .D({8{1'b0}}), .carry(counter_12_carry));  // open: count, Q
  Counter #(.max('h74)) counter_13 (
    .clr(1'b0), .load(1'b0), .up(1'b1), .clk(clock_1_out), .D({8{1'b0}}), .carry(counter_13_carry));  // open: count, Q
  Counter #(.max('h6e)) counter_14 (
    .clr(1'b0), .load(1'b0), .up(1'b1), .clk(clock_1_out), .D({8{1'b0}}), .carry(counter_14_carry));  // open: count, Q
  Counter #(.max('h68)) counter_15 (
    .clr(1'b0), .load(1'b0), .up(1'b1), .clk(clock_1_out), .D({8{1'b0}}), .carry(counter_15_carry));  // open: count, Q
  gated_clock_preventer gated_clock_preventer_5 (
    .input_1(counter_10_carry), .Q(d_ff_10_q), .Output_1(gated_clock_preventer_5_output_1));
  gated_clock_preventer gated_clock_preventer_7 (
    .input_1(counter_11_carry), .Q(d_ff_11_q), .Output_1(gated_clock_preventer_7_output_1));
  gated_clock_preventer gated_clock_preventer_9 (
    .input_1(counter_12_carry), .Q(d_ff_12_q), .Output_1(gated_clock_preventer_9_output_1));
  gated_clock_preventer gated_clock_preventer_10 (
    .input_1(counter_13_carry), .Q(d_ff_13_q), .Output_1(gated_clock_preventer_10_output_1));
  gated_clock_preventer gated_clock_preventer_12 (
    .input_1(counter_14_carry), .Q(d_ff_14_q), .Output_1(gated_clock_preventer_12_output_1));
  gated_clock_preventer gated_clock_preventer_14 (
    .input_1(counter_15_carry), .Q(d_ff_15_q), .Output_1(gated_clock_preventer_14_output_1));
  D_Flip_Flop d_ff_10 (
    .D(gated_clock_preventer_5_output_1), .clk(clock_1_out), .Q(d_ff_10_q), .preset(1'b0), .reset(1'b0));  // open: Qn
  D_Flip_Flop d_ff_11 (
    .D(gated_clock_preventer_7_output_1), .clk(clock_1_out), .Q(d_ff_11_q), .preset(1'b0), .reset(1'b0));  // open: Qn
  D_Flip_Flop d_ff_12 (
    .D(gated_clock_preventer_9_output_1), .clk(clock_1_out), .Q(d_ff_12_q), .preset(1'b0), .reset(1'b0));  // open: Qn
  D_Flip_Flop d_ff_13 (
    .D(gated_clock_preventer_10_output_1), .clk(clock_1_out), .Q(d_ff_13_q), .preset(1'b0), .reset(1'b0));  // open: Qn
  D_Flip_Flop d_ff_14 (
    .D(gated_clock_preventer_12_output_1), .clk(clock_1_out), .Q(d_ff_14_q), .preset(1'b0), .reset(1'b0));  // open: Qn
  D_Flip_Flop d_ff_15 (
    .D(gated_clock_preventer_14_output_1), .clk(clock_1_out), .Q(d_ff_15_q), .preset(1'b0), .reset(1'b0));  // open: Qn

  // Notes on the sheet:
  //   A
  //   divide by 2*nb_max=233
  //   As
  //   divide by 2*nb_max=220
  //   B
  //   divide by 2*nb_max=207
  //   C
  //   divide by 2*nb_max=196
  //   Cs
  //   divide by 2*nb_max=185
  //   D
  //   divide by 2*nb_max=174
  //   Ds
  //   divide by 2*nb_max=165
  //   E
  //   divide by 2*nb_max=155
  //   F
  //   divide by 2*nb_max=147
  //   Fs
  //   divide by 2*nb_max=238
  //   G
  //   divide by 2*nb_max=131
  //   Gs
  //   divide by 2*nb_max=128
  //   A2
  //   divide by 2*nb_max=116
  //   A2s
  //   divide by 2*nb_max=110
  //   B2
  //   divide by 2*nb_max=104
endmodule

module gated_clock_preventer (
  input  input_1,
  input  Q,
  output Output_1
);

  wire and_1_out, and_2_out, not_1_out, not_2_out;

  not not_1 (not_1_out, input_1);
  not not_2 (not_2_out, Q);
  and and_1 (and_1_out, not_1_out, Q);
  and and_2 (and_2_out, input_1, not_2_out);
  or or_1 (Output_1, and_1_out, and_2_out);
endmodule

module alarm_melody (
  input  alarm_on,
  output high
);

  wire clock_1_out, counter_1_carry, d_ff_1_q, d_ff_2_q, d_ff_3_q, d_ff_4_q, not_1_out, or_1_out,
       statemachine_melody_1_e0, statemachine_melody_1_e1, statemachine_melody_1_e2, statemachine_melody_1_e3;
  wire [2:0] statemachine_melody_1_d0;
  wire [3:0] statemachine_melody_1_n0;

  Clock #(.highDuration(17500), .lowDuration(17500)) clock_1 (.out(clock_1_out));
  statemachine_alarm_melody statemachine_melody_1 (
    .nextstate(counter_1_carry), .Etat3(d_ff_1_q), .Etat2(d_ff_2_q), .Etat1(d_ff_3_q), .Etat0(d_ff_4_q),
    .N3(statemachine_melody_1_n0[3]), .N2(statemachine_melody_1_n0[2]), .N1(statemachine_melody_1_n0[1]),
    .N0(statemachine_melody_1_n0[0]), .D2(statemachine_melody_1_d0[2]), .D1(statemachine_melody_1_d0[1]),
    .D0(statemachine_melody_1_d0[0]), .E3(statemachine_melody_1_e3), .E2(statemachine_melody_1_e2),
    .E1(statemachine_melody_1_e1), .E0(statemachine_melody_1_e0));
  D_Flip_Flop d_ff_1 (
    .D(statemachine_melody_1_e3), .clk(clock_1_out), .Q(d_ff_1_q), .reset(not_1_out));  // open: Qn, preset
  D_Flip_Flop d_ff_2 (
    .D(statemachine_melody_1_e2), .clk(clock_1_out), .Q(d_ff_2_q), .reset(not_1_out));  // open: Qn, preset
  D_Flip_Flop d_ff_3 (
    .D(statemachine_melody_1_e1), .clk(clock_1_out), .Q(d_ff_3_q), .reset(not_1_out));  // open: Qn, preset
  D_Flip_Flop d_ff_4 (
    .D(statemachine_melody_1_e0), .clk(clock_1_out), .Q(d_ff_4_q), .reset(not_1_out));  // open: Qn, preset
  frequency_generator frequency_generator_1 (.note(statemachine_melody_1_n0), .high(high));
  not not_1 (not_1_out, alarm_on);
  or or_1 (or_1_out, counter_1_carry, not_1_out);
  Counter #(.width(3), .max('h7), .ongoal("stay")) counter_1 (
    .clr(not_1_out), .load(or_1_out), .up(1'b0), .clk(clock_1_out), .D(statemachine_melody_1_d0),
    .carry(counter_1_carry));  // open: count, Q
endmodule

module statemachine_alarm_melody (
  input  nextstate,
  input  Etat3,
  input  Etat2,
  input  Etat1,
  input  Etat0,
  output N3,
  output N2,
  output N1,
  output N0,
  output D2,
  output D1,
  output D0,
  output E3,
  output E2,
  output E1,
  output E0
);

  wire and_1_out, and_2_out, and_3_out, and_4_out, and_5_out, and_6_out, and_7_out, and_8_out, and_9_out,
       and_10_out, and_11_out, and_12_out, and_13_out, and_14_out, and_15_out, and_16_out, and_17_out,
       and_18_out, and_19_out, and_20_out, and_21_out, and_22_out, and_23_out, and_24_out, and_25_out,
       and_26_out, and_27_out, and_28_out, and_29_out, and_30_out, and_31_out, and_32_out, and_33_out,
       and_34_out, and_35_out, and_36_out, and_37_out, and_38_out, and_39_out, and_40_out, and_41_out,
       and_42_out, and_43_out, and_44_out, and_45_out, and_46_out, and_47_out, and_48_out, and_49_out,
       and_50_out, and_51_out, and_52_out, and_53_out, and_54_out, and_55_out, and_56_out, and_57_out,
       and_58_out, and_59_out, and_60_out, not_1_out, not_2_out, not_3_out, not_4_out, not_5_out, not_6_out,
       not_7_out, not_8_out, not_9_out, not_10_out, not_11_out, not_12_out, not_13_out, not_14_out,
       not_15_out, not_16_out, not_17_out, not_18_out, not_19_out, not_20_out, not_21_out, not_22_out,
       not_23_out, not_24_out, not_25_out, not_26_out, not_27_out, not_28_out, not_29_out, not_30_out,
       not_31_out, not_32_out, not_33_out, not_34_out, not_35_out, not_36_out, not_37_out, not_38_out,
       not_39_out, not_40_out, not_41_out, not_42_out, not_43_out, not_44_out, not_45_out, not_46_out,
       not_47_out, not_48_out, not_49_out, not_50_out, not_51_out, not_52_out, not_53_out, not_54_out,
       not_55_out, not_56_out, not_57_out, not_58_out, not_59_out, not_60_out, not_61_out, not_62_out,
       not_63_out, not_64_out, not_65_out, not_66_out, not_67_out, not_68_out, not_69_out, not_70_out,
       not_71_out, not_72_out, not_73_out, not_74_out, not_75_out, not_76_out, not_77_out, not_78_out,
       not_79_out, not_80_out, not_81_out, not_82_out, not_83_out, not_84_out, not_85_out, not_86_out,
       not_87_out, not_88_out, not_89_out, not_90_out, not_91_out, not_92_out, not_93_out, not_94_out,
       not_95_out, not_96_out, not_97_out, not_98_out, not_99_out, not_100_out, not_101_out, not_102_out,
       not_103_out;

  not not_1 (not_1_out, Etat3);
  not not_2 (not_2_out, Etat3);
  not not_3 (not_3_out, Etat2);
  not not_4 (not_4_out, Etat1);
  not not_5 (not_5_out, Etat3);
  not not_6 (not_6_out, Etat1);
  not not_7 (not_7_out, Etat0);
  not not_8 (not_8_out, Etat3);
  not not_9 (not_9_out, Etat2);
  not not_10 (not_10_out, Etat0);
  not not_11 (not_11_out, Etat0);
  not not_12 (not_12_out, Etat2);
  not not_13 (not_13_out, Etat3);
  not not_14 (not_14_out, Etat2);
  not not_15 (not_15_out, Etat3);
  not not_16 (not_16_out, Etat0);
  not not_17 (not_17_out, Etat1);
  not not_18 (not_18_out, nextstate);
  not not_19 (not_19_out, Etat3);
  not not_20 (not_20_out, nextstate);
  not not_21 (not_21_out, Etat1);
  not not_22 (not_22_out, Etat0);
  not not_23 (not_23_out, nextstate);
  not not_24 (not_24_out, Etat0);
  not not_25 (not_25_out, Etat3);
  not not_26 (not_26_out, Etat0);
  not not_27 (not_27_out, Etat3);
  not not_28 (not_28_out, Etat2);
  not not_29 (not_29_out, Etat1);
  not not_30 (not_30_out, Etat3);
  not not_31 (not_31_out, Etat2);
  not not_32 (not_32_out, Etat1);
  not not_33 (not_33_out, nextstate);
  not not_34 (not_34_out, Etat3);
  not not_35 (not_35_out, Etat0);
  not not_36 (not_36_out, nextstate);
  not not_37 (not_37_out, Etat3);
  not not_38 (not_38_out, Etat0);
  not not_39 (not_39_out, nextstate);
  not not_40 (not_40_out, Etat2);
  not not_41 (not_41_out, nextstate);
  not not_42 (not_42_out, Etat1);
  not not_43 (not_43_out, Etat3);
  not not_44 (not_44_out, Etat2);
  not not_45 (not_45_out, Etat1);
  not not_46 (not_46_out, Etat3);
  not not_47 (not_47_out, Etat2);
  not not_48 (not_48_out, Etat3);
  not not_49 (not_49_out, Etat1);
  not not_50 (not_50_out, Etat2);
  not not_51 (not_51_out, Etat0);
  not not_52 (not_52_out, Etat1);
  not not_53 (not_53_out, Etat0);
  not not_54 (not_54_out, nextstate);
  not not_55 (not_55_out, Etat2);
  not not_56 (not_56_out, Etat0);
  not not_57 (not_57_out, nextstate);
  not not_58 (not_58_out, Etat3);
  not not_59 (not_59_out, Etat2);
  not not_60 (not_60_out, Etat1);
  not not_61 (not_61_out, Etat0);
  not not_62 (not_62_out, Etat2);
  not not_63 (not_63_out, Etat1);
  not not_64 (not_64_out, Etat3);
  not not_65 (not_65_out, Etat0);
  not not_66 (not_66_out, Etat3);
  not not_67 (not_67_out, Etat1);
  not not_68 (not_68_out, nextstate);
  not not_69 (not_69_out, Etat0);
  not not_70 (not_70_out, Etat2);
  not not_71 (not_71_out, Etat1);
  not not_72 (not_72_out, Etat3);
  not not_73 (not_73_out, nextstate);
  not not_74 (not_74_out, Etat3);
  not not_75 (not_75_out, nextstate);
  not not_76 (not_76_out, Etat0);
  not not_77 (not_77_out, Etat3);
  not not_78 (not_78_out, Etat0);
  not not_79 (not_79_out, Etat1);
  not not_80 (not_80_out, Etat2);
  not not_81 (not_81_out, nextstate);
  not not_82 (not_82_out, Etat3);
  not not_83 (not_83_out, nextstate);
  not not_84 (not_84_out, Etat2);
  not not_85 (not_85_out, nextstate);
  not not_86 (not_86_out, Etat0);
  not not_87 (not_87_out, Etat3);
  not not_88 (not_88_out, Etat0);
  not not_89 (not_89_out, Etat2);
  not not_90 (not_90_out, Etat0);
  not not_91 (not_91_out, Etat1);
  not not_92 (not_92_out, nextstate);
  not not_93 (not_93_out, Etat3);
  not not_94 (not_94_out, nextstate);
  not not_95 (not_95_out, Etat2);
  not not_96 (not_96_out, nextstate);
  not not_97 (not_97_out, Etat1);
  not not_98 (not_98_out, Etat3);
  not not_99 (not_99_out, Etat0);
  not not_100 (not_100_out, Etat2);
  not not_101 (not_101_out, Etat0);
  not not_102 (not_102_out, Etat1);
  not not_103 (not_103_out, Etat0);
  and and_1 (and_1_out, not_1_out, Etat1);
  and and_2 (and_2_out, not_2_out, Etat2);
  and and_3 (and_3_out, Etat3, not_3_out);
  and and_4 (and_4_out, Etat3, not_4_out, Etat0);
  and and_5 (and_5_out, not_5_out, Etat2, Etat1);
  and and_6 (and_6_out, Etat3, Etat2, not_6_out, not_7_out);
  and and_7 (and_7_out, not_8_out, not_9_out, Etat0);
  and and_8 (and_8_out, Etat2, not_10_out);
  and and_9 (and_9_out, Etat3, not_11_out);
  and and_10 (and_10_out, Etat3, not_12_out, Etat1);
  and and_11 (and_11_out, not_13_out, not_14_out, Etat0);
  and and_12 (and_12_out, not_15_out, Etat2, Etat1);
  and and_13 (and_13_out, Etat3, Etat1, not_16_out);
  and and_14 (and_14_out, Etat3, Etat2, not_17_out);
  and and_15 (and_15_out, not_18_out, not_19_out, Etat2, Etat0);
  and and_16 (and_16_out, not_20_out, Etat3, not_21_out, not_22_out);
  and and_17 (and_17_out, not_23_out, Etat3, Etat2, not_24_out);
  and and_18 (and_18_out, nextstate, not_25_out, Etat2, not_26_out);
  and and_19 (and_19_out, nextstate, not_27_out, Etat2, Etat1);
  and and_20 (and_20_out, nextstate, Etat3, not_28_out, Etat1, Etat0);
  and and_21 (and_21_out, nextstate, Etat3, Etat2, not_29_out, Etat0);
  and and_22 (and_22_out, not_30_out, not_31_out, not_32_out, Etat0);
  and and_23 (and_23_out, not_33_out, not_34_out, Etat1, not_35_out);
  and and_24 (and_24_out, not_36_out, not_37_out, Etat2, not_38_out);
  and and_25 (and_25_out, not_39_out, Etat3, not_40_out, Etat0);
  and and_26 (and_26_out, not_41_out, Etat3, not_42_out, Etat0);
  and and_27 (and_27_out, nextstate, not_43_out, not_44_out, not_45_out);
  and and_28 (and_28_out, nextstate, not_46_out, not_47_out, Etat0);
  and and_29 (and_29_out, nextstate, not_48_out, not_49_out, Etat0);
  and and_30 (and_30_out, nextstate, Etat3, not_50_out, not_51_out);
  and and_31 (and_31_out, nextstate, Etat3, not_52_out, not_53_out);
  and and_32 (and_32_out, not_54_out, not_55_out, not_56_out);
  and and_33 (and_33_out, not_57_out, not_58_out, Etat1, Etat0);
  and and_34 (and_34_out, Etat3, not_59_out, not_60_out);
  and and_35 (and_35_out, Etat3, Etat2, Etat1, not_61_out);
  and and_36 (and_36_out, nextstate, not_62_out, not_63_out, Etat0);
  and and_37 (and_37_out, nextstate, not_64_out, Etat1, not_65_out);
  and and_38 (and_38_out, nextstate, not_66_out, Etat2, Etat1);
  and and_39 (and_39_out, nextstate, Etat3, not_67_out, Etat0);
  and and_40 (and_40_out, not_68_out, Etat3, not_69_out);
  and and_41 (and_41_out, Etat3, not_70_out);
  and and_42 (and_42_out, Etat3, not_71_out);
  and and_43 (and_43_out, nextstate, not_72_out, Etat2, Etat1, Etat0);
  and and_44 (and_44_out, not_73_out, not_74_out, Etat2);
  and and_45 (and_45_out, not_75_out, Etat2, not_76_out);
  and and_46 (and_46_out, not_77_out, Etat2, not_78_out);
  and and_47 (and_47_out, Etat2, not_79_out);
  and and_48 (and_48_out, nextstate, not_80_out, Etat1, Etat0);
  and and_49 (and_49_out, not_81_out, not_82_out, Etat1);
  and and_50 (and_50_out, not_83_out, not_84_out, Etat1);
  and and_51 (and_51_out, not_85_out, Etat1, not_86_out);
  and and_52 (and_52_out, not_87_out, Etat1, not_88_out);
  and and_53 (and_53_out, not_89_out, Etat1, not_90_out);
  and and_54 (and_54_out, nextstate, not_91_out, Etat0);
  and and_55 (and_55_out, not_92_out, not_93_out, Etat0);
  and and_56 (and_56_out, not_94_out, not_95_out, Etat0);
  and and_57 (and_57_out, not_96_out, not_97_out, Etat0);
  and and_58 (and_58_out, nextstate, not_98_out, not_99_out);
  and and_59 (and_59_out, nextstate, not_100_out, not_101_out);
  and and_60 (and_60_out, nextstate, not_102_out, not_103_out);
  or or_1 (N3, and_1_out, and_2_out, and_3_out, and_4_out);
  or or_2 (N2, and_5_out, and_6_out);
  or or_3 (N1, and_7_out, and_8_out, and_9_out, and_10_out);
  or or_4 (N0, and_11_out, and_12_out, and_13_out, and_14_out);
  or or_5 (D2, and_15_out, and_16_out, and_17_out, and_18_out, and_19_out, and_20_out, and_21_out);
  or or_6 (D0, and_32_out, and_33_out, and_34_out, and_35_out, and_36_out, and_37_out, and_38_out, and_39_out);
  or or_7 (E3, and_40_out, and_41_out, and_42_out, and_43_out);
  or or_8 (E2, and_44_out, and_45_out, and_46_out, and_47_out, and_48_out);
  or or_9 (E1, and_49_out, and_50_out, and_51_out, and_52_out, and_53_out, and_54_out);
  or or_10 (E0, and_55_out, and_56_out, and_57_out, and_58_out, and_59_out, and_60_out);
  or or_11 (D1, and_22_out, and_23_out, and_24_out, and_25_out, and_26_out, and_27_out, and_28_out, and_29_out, and_30_out, and_31_out);
endmodule

module binary_to_display_code (
  input  b0,
  input  b1,
  input  b2,
  input  b3,
  output a,
  output b,
  output c,
  output d,
  output e,
  output f,
  output g
);

  wire and_1_out, and_2_out, and_3_out, and_4_out, and_5_out, and_6_out, and_7_out, and_8_out, and_9_out,
       and_10_out, and_11_out, and_12_out, and_13_out, and_14_out, and_15_out, and_16_out, and_17_out,
       and_18_out, and_19_out, and_20_out, and_21_out, and_22_out, and_23_out, and_24_out, and_25_out,
       and_26_out, and_27_out, and_28_out, and_29_out, and_30_out, and_31_out, and_32_out, and_33_out,
       and_34_out, and_35_out, not_1_out, not_2_out, not_3_out, not_4_out, not_5_out, not_6_out, not_7_out,
       not_8_out, not_9_out, not_10_out, not_11_out, not_12_out, not_13_out, not_14_out, not_15_out,
       not_16_out, not_17_out, not_18_out, not_19_out, not_20_out, not_21_out, not_22_out, not_23_out,
       not_24_out, not_25_out, not_26_out, not_27_out, not_28_out, not_29_out, not_30_out, not_31_out,
       not_32_out, not_33_out, not_34_out, not_35_out, not_36_out, not_37_out, not_38_out, not_39_out,
       not_40_out, not_41_out, not_42_out, not_43_out;

  not not_1 (not_1_out, b2);
  not not_2 (not_2_out, b0);
  not not_3 (not_3_out, b3);
  not not_4 (not_4_out, b3);
  not not_5 (not_5_out, b2);
  not not_6 (not_6_out, b1);
  not not_7 (not_7_out, b0);
  not not_8 (not_8_out, b0);
  not not_9 (not_9_out, b1);
  not not_10 (not_10_out, b3);
  not not_11 (not_11_out, b0);
  not not_12 (not_12_out, b2);
  not not_13 (not_13_out, b1);
  not not_14 (not_14_out, b2);
  not not_15 (not_15_out, b1);
  not not_16 (not_16_out, b3);
  not not_17 (not_17_out, b1);
  not not_18 (not_18_out, b2);
  not not_19 (not_19_out, b2);
  not not_20 (not_20_out, b3);
  not not_21 (not_21_out, b1);
  not not_22 (not_22_out, b2);
  not not_23 (not_23_out, b0);
  not not_24 (not_24_out, b2);
  not not_25 (not_25_out, b3);
  not not_26 (not_26_out, b1);
  not not_27 (not_27_out, b0);
  not not_28 (not_28_out, b1);
  not not_29 (not_29_out, b2);
  not not_30 (not_30_out, b0);
  not not_31 (not_31_out, b2);
  not not_32 (not_32_out, b0);
  not not_33 (not_33_out, b0);
  not not_34 (not_34_out, b1);
  not not_35 (not_35_out, b2);
  not not_36 (not_36_out, b0);
  not not_37 (not_37_out, b1);
  not not_38 (not_38_out, b3);
  not not_39 (not_39_out, b2);
  not not_40 (not_40_out, b1);
  not not_41 (not_41_out, b3);
  not not_42 (not_42_out, b0);
  not not_43 (not_43_out, b2);
  and and_1 (and_1_out, not_1_out, not_2_out);
  and and_2 (and_2_out, not_3_out, b1);
  and and_3 (and_3_out, not_4_out, b2, b0);
  and and_4 (and_4_out, b2, b1);
  and and_5 (and_5_out, b3, not_5_out, not_6_out);
  and and_6 (and_6_out, b3, not_7_out);
  and and_7 (and_7_out, not_8_out, not_9_out, not_10_out);
  and and_8 (and_8_out, not_11_out, not_12_out);
  and and_9 (and_9_out, not_13_out, not_14_out);
  and and_10 (and_10_out, b0, not_15_out, b3);
  and and_11 (and_11_out, b0, b1, not_16_out);
  and and_12 (and_12_out, not_17_out, not_18_out);
  and and_13 (and_13_out, not_19_out, b3);
  and and_14 (and_14_out, b2, not_20_out);
  and and_15 (and_15_out, b0, not_21_out);
  and and_16 (and_16_out, b0, not_22_out);
  and and_17 (and_17_out, not_23_out, not_24_out, not_25_out);
  and and_18 (and_18_out, not_26_out, b3);
  and and_19 (and_19_out, not_27_out, b1, b2);
  and and_20 (and_20_out, b0, not_28_out, b2);
  and and_21 (and_21_out, b0, b1, not_29_out);
  and and_22 (and_22_out, not_30_out, not_31_out);
  and and_23 (and_23_out, b2, b3);
  and and_24 (and_24_out, not_32_out, b1);
  and and_25 (and_25_out, b1, b3);
  and and_26 (and_26_out, not_33_out, not_34_out);
  and and_27 (and_27_out, not_35_out, b3);
  and and_28 (and_28_out, not_36_out, b2);
  and and_29 (and_29_out, not_37_out, b2, not_38_out);
  and and_30 (and_30_out, b1, b3);
  and and_31 (and_31_out, not_39_out, b3);
  and and_32 (and_32_out, not_40_out, b2, not_41_out);
  and and_33 (and_33_out, not_42_out, b1);
  and and_34 (and_34_out, b1, not_43_out);
  and and_35 (and_35_out, b0, b3);
  or or_1 (a, and_1_out, and_2_out, and_3_out, and_4_out, and_5_out, and_6_out);
  or or_2 (b, and_7_out, and_8_out, and_9_out, and_10_out, and_11_out);
  or or_3 (c, and_12_out, and_13_out, and_14_out, and_15_out, and_16_out);
  or or_4 (d, and_17_out, and_18_out, and_19_out, and_20_out, and_21_out);
  or or_5 (e, and_22_out, and_23_out, and_24_out, and_25_out);
  or or_6 (f, and_26_out, and_27_out, and_28_out, and_29_out, and_30_out);
  or or_7 (g, and_31_out, and_32_out, and_33_out, and_34_out, and_35_out);
endmodule

module time_comparator (
  input  [6:0] alarm_s1,
  input  [6:0] alarm_s2,
  input  [6:0] alarm_m1,
  input  [6:0] alarm_m2,
  input  [6:0] alarm_h1,
  input  [6:0] alarm_h2,
  input  [6:0] clock_s1,
  input  [6:0] clock_s2,
  input  [6:0] clock_m1,
  input  [6:0] clock_m2,
  input  [6:0] clock_h1,
  input  [6:0] clock_h2,
  input  alarm_on,
  output alarm
);

  wire and_2_out, and_5_out;
  wire [6:0] and_1_out, and_4_out, xnor_1_out, xnor_2_out, xnor_3_out, xnor_4_out, xnor_5_out, xnor_6_out;

  assign xnor_1_out = ~(clock_m1 ^ alarm_m1);  // XNOR_Gate xnor_1, 7 bits wide
  assign xnor_2_out = ~(clock_m2 ^ alarm_m2);  // XNOR_Gate xnor_2, 7 bits wide
  assign xnor_3_out = ~(clock_h1 ^ alarm_h1);  // XNOR_Gate xnor_3, 7 bits wide
  assign and_1_out = xnor_1_out & xnor_2_out & xnor_3_out & xnor_4_out;  // AND_Gate and_1, 7 bits wide
  assign xnor_4_out = ~(clock_h2 ^ alarm_h2);  // XNOR_Gate xnor_4, 7 bits wide
  and and_2 (and_2_out, and_1_out[6], and_1_out[5], and_1_out[4], and_1_out[3], and_1_out[2], and_1_out[1], and_1_out[0]);
  and and_3 (alarm, and_2_out, alarm_on, and_5_out);
  assign xnor_5_out = ~(clock_s1 ^ alarm_s1);  // XNOR_Gate xnor_5, 7 bits wide
  assign xnor_6_out = ~(clock_s2 ^ alarm_s2);  // XNOR_Gate xnor_6, 7 bits wide
  assign and_4_out = xnor_5_out & xnor_6_out;  // AND_Gate and_4, 7 bits wide
  and and_5 (and_5_out, and_4_out[6], and_4_out[5], and_4_out[4], and_4_out[3], and_4_out[2], and_4_out[1], and_4_out[0]);
endmodule

module adder_1bit (
  input  A,
  input  B,
  input  Carry_in,
  output P,
  output Carry
);

  wire and_1_out, and_2_out, and_3_out, and_4_out, and_5_out, and_6_out, and_7_out, not_1_out, not_2_out,
       not_3_out, not_4_out, not_5_out, not_6_out;

  not not_1 (not_1_out, A);
  not not_2 (not_2_out, B);
  and and_1 (and_1_out, not_1_out, not_2_out, Carry_in);
  not not_3 (not_3_out, A);
  and and_2 (and_2_out, not_3_out, B, not_4_out);
  not not_4 (not_4_out, Carry_in);
  not not_5 (not_5_out, B);
  and and_3 (and_3_out, A, not_5_out, not_6_out);
  not not_6 (not_6_out, Carry_in);
  and and_4 (and_4_out, A, B, Carry_in);
  and and_5 (and_5_out, B, Carry_in);
  and and_6 (and_6_out, A, Carry_in);
  and and_7 (and_7_out, A, B);
  or or_1 (P, and_1_out, and_2_out, and_3_out, and_4_out);
  or or_2 (Carry, and_5_out, and_6_out, and_7_out);
endmodule

module adder_5bit (
  input  Carry_in,
  input  [4:0] A,
  input  [4:0] B,
  output [4:0] P,
  output Carry_out
);

  wire adder_1bit_1_carry, adder_1bit_2_carry, adder_1bit_3_carry, adder_1bit_4_carry;

  adder_1bit adder_1bit_1 (.A(A[0]), .B(B[0]), .Carry_in(Carry_in), .P(P[0]), .Carry(adder_1bit_1_carry));
  adder_1bit adder_1bit_2 (.A(A[1]), .B(B[1]), .Carry_in(adder_1bit_1_carry), .P(P[1]), .Carry(adder_1bit_2_carry));
  adder_1bit adder_1bit_3 (.A(A[2]), .B(B[2]), .Carry_in(adder_1bit_2_carry), .P(P[2]), .Carry(adder_1bit_3_carry));
  adder_1bit adder_1bit_4 (.A(A[3]), .B(B[3]), .Carry_in(adder_1bit_3_carry), .P(P[3]), .Carry(adder_1bit_4_carry));
  adder_1bit adder_1bit_5 (.A(A[4]), .B(B[4]), .Carry_in(adder_1bit_4_carry), .P(P[4]), .Carry(Carry_out));
endmodule

module substractor_1bit (
  input  A,
  input  B,
  input  Carry_in,
  output M,
  output Carry
);

  wire and_1_out, and_2_out, and_3_out, and_4_out, and_5_out, and_6_out, and_7_out, not_1_out, not_2_out,
       not_3_out, not_4_out, not_5_out, not_6_out, not_7_out, not_8_out;

  not not_1 (not_1_out, A);
  not not_2 (not_2_out, B);
  not not_3 (not_3_out, A);
  not not_4 (not_4_out, Carry_in);
  not not_5 (not_5_out, B);
  not not_6 (not_6_out, Carry_in);
  not not_7 (not_7_out, A);
  not not_8 (not_8_out, A);
  and and_1 (and_1_out, not_1_out, not_2_out, Carry_in);
  and and_2 (and_2_out, not_3_out, B, not_4_out);
  and and_3 (and_3_out, A, not_5_out, not_6_out);
  and and_4 (and_4_out, A, B, Carry_in);
  and and_5 (and_5_out, not_7_out, Carry_in);
  and and_6 (and_6_out, not_8_out, B);
  and and_7 (and_7_out, B, Carry_in);
  or or_1 (M, and_1_out, and_2_out, and_3_out, and_4_out);
  or or_2 (Carry, and_5_out, and_6_out, and_7_out);
endmodule

module substractor_5bit (
  input  carry_in,
  input  [4:0] A,
  input  [4:0] B,
  output [4:0] P,
  output carry_out
);

  wire substractor_1bit_1_carry, substractor_1bit_2_carry, substractor_1bit_3_carry, substractor_1bit_4_carry;

  substractor_1bit substractor_1bit_1 (
    .A(A[0]), .B(B[0]), .Carry_in(carry_in), .M(P[0]), .Carry(substractor_1bit_1_carry));
  substractor_1bit substractor_1bit_2 (
    .A(A[1]), .B(B[1]), .Carry_in(substractor_1bit_1_carry), .M(P[1]), .Carry(substractor_1bit_2_carry));
  substractor_1bit substractor_1bit_3 (
    .A(A[2]), .B(B[2]), .Carry_in(substractor_1bit_2_carry), .M(P[2]), .Carry(substractor_1bit_3_carry));
  substractor_1bit substractor_1bit_4 (
    .A(A[3]), .B(B[3]), .Carry_in(substractor_1bit_3_carry), .M(P[3]), .Carry(substractor_1bit_4_carry));
  substractor_1bit substractor_1bit_5 (
    .A(A[4]), .B(B[4]), .Carry_in(substractor_1bit_4_carry), .M(P[4]), .Carry(carry_out));
endmodule
